// Logisim project Control.circ as structural Verilog: 2 circuits, main circuit main
module main (
  input  [3:0] in_1,
  output out_2,
  output out_3,
  output out_4,
  output [3:0] out_5,
  output out_6,
  output out_7,
  output out_8,
  output out_9,
  output out_10
);

  ControlSignal controlsignal_1 (
    .OpCode(in_1), .ALUOpCode(out_5), .Branch(out_6), .MemRead(out_7), .MemToReg(out_8), .ALUSrc(out_9),
    .RegDst(out_10), .Jump(out_2), .MemWrite(out_3), .RegWrite(out_4));  // open: Overall_Output
endmodule

module ControlSignal (
  input  [3:0] OpCode,
  output [11:0] Overall_Output,
  output Jump,
  output [3:0] ALUOpCode,
  output Branch,
  output MemWrite,
  output MemRead,
  output RegWrite,
  output MemToReg,
  output ALUSrc,
  output RegDst
);

  ROM #(.addrWidth(4), .dataWidth(12)) rom_1 (
    .addr(OpCode),
    .data({Overall_Output[11], ALUSrc, MemToReg, Overall_Output[8], MemRead, MemWrite, Branch, ALUOpCode, Jump}));  // open: sel

  assign {Overall_Output[10:9], Overall_Output[7:0]} = {ALUSrc, MemToReg, MemRead, MemWrite, Branch, ALUOpCode, Jump};
  assign RegDst = Overall_Output[11];
  assign RegWrite = Overall_Output[8];

  // Notes on the sheet:
  //   contents of rom_1 (hex, n*v repeats v):
  //   0 900 500 902 502 90c 50c 444 784 904 504 2c 1
endmodule
