// Logisim project ID_SUBcircuit.circ as structural Verilog: 3 circuits, main circuit main
module main (
  input  [3:0] in_1,
  input  [15:0] in_2,
  input  in_3,
  input  in_4,
  output [3:0] out_5,
  output [3:0] out_6,
  output [3:0] out_7,
  output [3:0] out_8
);

  instruction instruction_1 ();  // open: in_1, in_2, in_3, in_4, out_6, out_7, out_8, out_9, Clk
endmodule

module fr (
  input  in_1,
  input  in_2,
  input  in_3,
  output out_4
);

  and and_1 (out_4, in_1, in_2, in_3);
endmodule

module instruction (
  input  [3:0] in_1,
  input  [15:0] in_2,
  input  in_3,
  input  in_4,
  input  Clk,
  output [3:0] out_6,
  output [3:0] out_7,
  output [3:0] out_8,
  output [3:0] out_9
);

  RAM #(.addrWidth(4), .dataWidth(16), .bus("separate")) ram_1 (
    .addr(in_1), .din(in_2), .data({out_9, out_8, out_7, out_6}), .str(in_3), .clk(Clk), .ld(in_4));  // open: sel, clr

  // Notes on the sheet:
  //   data
  //   address
endmodule
