// Logisim project RAM.circ as structural Verilog: 1 circuit, main circuit main
module main (
  input  in_1,
  input  in_2,
  output out_3,
  output out_4,
  output out_5,
  output out_6
);

  wire clock_1_out;

  ROM rom_1 ();  // open: addr, data, sel
  Clock clock_1 (.out(clock_1_out));
  RAM #(.addrWidth(4), .dataWidth(4), .bus("separate")) ram_1 (
    .addr(4'b1110), .data({out_6, out_5, out_4, out_3}), .str(in_1), .clk(clock_1_out), .ld(in_2));  // open: din, sel, clr
endmodule
