// Logisim project ALU.circ as structural Verilog: 2 circuits, main circuit main
module main (
);

  wire A0, A1, A2, A3, Ad0, Ad1, Ad2, Ad3, adder_1_out_10, adder_1_out_11, adder_1_out_12, adder_1_out_13,
       and_1_out, and_2_out, and_3_out, and_4_out, B0, B1, B2, B3, C0, C1, C2, C3, C4, CIN, clock_1_out, go,
       not_1_out, not_2_out, not_3_out, not_4_out, or_1_out, or_2_out, or_3_out, or_4_out, Reset_out, S0, S1,
       t_ff_1_q, t_ff_2_q, t_ff_3_q, t_ff_4_q;
  wire [11:11] rom_1_data;

  Clock clock_1 (.out(clock_1_out));
  T_Flip_Flop t_ff_1 (.clk(clock_1_out), .T(1'b1), .Q(t_ff_1_q), .Qn(Ad0), .preset(Reset_out), .en(go));  // open: reset
  // Probe on {C4, C3, C2, C1, C0}
  T_Flip_Flop t_ff_2 (.clk(t_ff_1_q), .T(1'b1), .Q(t_ff_2_q), .Qn(Ad1), .preset(Reset_out));  // open: reset, en
  // Probe on CIN
  // Probe on {S1, S0}
  TTY #(.rows(1), .cols(16)) tty_1 (.data({2'b10, C4, C3, C2, C1, C0}), .clk(clock_1_out), .we(go), .clr(Reset_out));
  T_Flip_Flop t_ff_3 (.clk(t_ff_2_q), .T(1'b1), .Q(t_ff_3_q), .Qn(Ad2), .preset(Reset_out));  // open: reset, en
  // Probe on {rom_1_data[11], CIN, S1, S0, B3, B2, B1, B0, A3, A2, A1, A0}
  ROM #(.addrWidth(4), .dataWidth(12)) rom_1 (
    .addr({Ad3, Ad2, Ad1, Ad0}), .data({rom_1_data[11], CIN, S1, S0, B3, B2, B1, B0, A3, A2, A1, A0}));  // open: sel
  // Probe on {B3, B2, B1, B0}
  T_Flip_Flop t_ff_4 (.clk(t_ff_3_q), .T(1'b1), .Q(t_ff_4_q), .Qn(Ad3), .preset(Reset_out));  // open: reset, en
  T_Flip_Flop t_ff_5 (.clk(t_ff_4_q), .T(1'b1), .Q(go), .preset(Reset_out));  // open: Qn, reset, en
  // Probe on {A3, A2, A1, A0}
  Button Reset (.out(Reset_out));
  and and_1 (and_1_out, B3, A3);
  and and_2 (and_2_out, B2, A2);
  and and_3 (and_3_out, B1, A1);
  and and_4 (and_4_out, B0, A0);
  or or_1 (or_1_out, B3, A3);
  Multiplexer #(.select(2)) multiplexer_1 (
    .in0(and_1_out), .in1(or_1_out), .in2(not_1_out), .in3(adder_1_out_13), .out(C3), .sel({S1, S0}));  // open: en
  or or_2 (or_2_out, B2, A2);
  Multiplexer #(.select(2)) multiplexer_2 (
    .in0(and_2_out), .in1(or_2_out), .in2(not_2_out), .in3(adder_1_out_12), .out(C2), .sel({S1, S0}));  // open: en
  or or_3 (or_3_out, B1, A1);
  Multiplexer #(.select(2)) multiplexer_3 (
    .in0(and_3_out), .in1(or_3_out), .in2(not_4_out), .in3(adder_1_out_11), .out(C1), .sel({S1, S0}));  // open: en
  or or_4 (or_4_out, B0, A0);
  Multiplexer #(.select(2)) multiplexer_4 (
    .in0(and_4_out), .in1(or_4_out), .in2(not_3_out), .in3(adder_1_out_10), .out(C0), .sel({S1, S0}));  // open: en
  not not_1 (not_1_out, A3);
  not not_2 (not_2_out, A2);
  not not_3 (not_3_out, A0);
  not not_4 (not_4_out, A1);
  adder adder_1 (
    .in_1(A0), .in_2(B0), .in_3(CIN), .in_4(A1), .in_5(B1), .in_6(A2), .in_7(B2), .in_8(A3), .in_9(B3),
    .out_10(adder_1_out_10), .out_11(adder_1_out_11), .out_12(adder_1_out_12), .out_13(adder_1_out_13),
    .out_14(C4));

  // Notes on the sheet:
  //   adds 64 to make printable
  //   contents of rom_1 (hex, n*v repeats v):
  //   0 4ff ac 100 5ff 1ac 200 6ff 2ac 300 7ff 3ac 3c3 73c 37d 7d7
  //   @_X@_^OPS@_VOPTU
endmodule

// Adder
module adder (
  input  in_1,
  input  in_2,
  input  in_3,
  input  in_4,
  input  in_5,
  input  in_6,
  input  in_7,
  input  in_8,
  input  in_9,
  output out_10,
  output out_11,
  output out_12,
  output out_13,
  output out_14
);

  wire and_1_out, and_2_out, and_3_out, and_4_out, and_5_out, and_6_out, and_7_out, and_8_out, C0Temp,
       C1Temp, C2Temp, xor_1_out, xor_2_out, xor_3_out, xor_4_out;

  xor xor_1 (xor_1_out, in_8, in_9);
  xor xor_2 (xor_2_out, in_1, in_2);
  and and_1 (and_1_out, in_1, in_2);
  xor xor_3 (xor_3_out, in_4, in_5);
  and and_2 (and_2_out, in_4, in_5);
  xor xor_4 (xor_4_out, in_6, in_7);
  and and_3 (and_3_out, in_6, in_7);
  and and_4 (and_4_out, in_8, in_9);
  xor xor_5 (out_10, xor_2_out, in_3);
  and and_5 (and_5_out, xor_2_out, in_3);
  xor xor_6 (out_11, xor_3_out, C0Temp);
  and and_6 (and_6_out, xor_3_out, C0Temp);
  xor xor_7 (out_12, xor_4_out, C1Temp);
  and and_7 (and_7_out, xor_4_out, C1Temp);
  xor xor_8 (out_13, xor_1_out, C2Temp);
  and and_8 (and_8_out, xor_1_out, C2Temp);
  or or_1 (C0Temp, and_5_out, and_1_out);
  or or_2 (C1Temp, and_6_out, and_2_out);
  or or_3 (C2Temp, and_7_out, and_3_out);
  or or_4 (out_14, and_8_out, and_4_out);
endmodule
