// Logisim project 16-reg_file.circ as structural Verilog: 2 circuits, main circuit main
module main (
  input  [15:0] \input ,
  input  [3:0] write_register,
  input  [3:0] read_register_0,
  input  single_reg_instr,
  input  [3:0] read_register_1,
  input  write,
  output [15:0] output_0,
  output [15:0] output_1
);

  wire and_1_out, and_2_out, and_3_out, and_4_out, and_5_out, and_6_out, and_7_out, and_8_out, and_9_out,
       and_10_out, and_11_out, and_12_out, and_13_out, and_14_out, and_15_out, and_16_out, not_1_out,
       not_2_out, not_3_out, not_4_out, not_5_out, not_6_out, not_7_out, not_8_out, not_9_out, not_10_out,
       not_11_out, not_12_out, not_13_out, not_14_out, not_15_out, not_16_out, not_17_out, not_18_out,
       not_19_out, not_20_out, not_21_out, not_22_out, not_23_out, not_24_out, not_25_out, not_26_out,
       not_27_out, not_28_out, not_29_out, not_30_out, not_31_out, not_32_out;
  wire [3:0] multiplexer_2_out;
  wire [15:0] register_1_q, register_2_q, register_3_q, register_4_q, register_5_q, register_6_q,
       register_7_q, register_8_q, register_9_q, register_10_q, register_11_q, register_12_q, register_13_q,
       register_14_q, register_15_q, register_16_q;

  not not_1 (not_1_out, write_register[0]);
  not not_2 (not_2_out, write_register[1]);
  not not_3 (not_3_out, write_register[2]);
  not not_4 (not_4_out, write_register[3]);
  not not_5 (not_5_out, write_register[1]);
  not not_6 (not_6_out, write_register[2]);
  not not_7 (not_7_out, write_register[3]);
  not not_8 (not_8_out, write_register[0]);
  not not_9 (not_9_out, write_register[2]);
  not not_10 (not_10_out, write_register[3]);
  not not_11 (not_11_out, write_register[2]);
  not not_12 (not_12_out, write_register[3]);
  not not_13 (not_13_out, write_register[0]);
  not not_14 (not_14_out, write_register[1]);
  not not_15 (not_15_out, write_register[3]);
  not not_16 (not_16_out, write_register[1]);
  not not_17 (not_17_out, write_register[3]);
  not not_18 (not_18_out, write_register[0]);
  not not_19 (not_19_out, write_register[3]);
  not not_20 (not_20_out, write_register[3]);
  not not_21 (not_21_out, write_register[0]);
  not not_22 (not_22_out, write_register[1]);
  not not_23 (not_23_out, write_register[2]);
  not not_24 (not_24_out, write_register[1]);
  not not_25 (not_25_out, write_register[2]);
  not not_26 (not_26_out, write_register[0]);
  not not_27 (not_27_out, write_register[2]);
  not not_28 (not_28_out, write_register[2]);
  not not_29 (not_29_out, write_register[0]);
  not not_30 (not_30_out, write_register[1]);
  not not_31 (not_31_out, write_register[1]);
  not not_32 (not_32_out, write_register[0]);
  and and_1 (and_1_out, not_1_out, not_2_out, not_3_out, not_4_out, write);
  and and_2 (and_2_out, write_register[0], not_5_out, not_6_out, not_7_out, write);
  and and_3 (and_3_out, not_8_out, write_register[1], not_9_out, not_10_out, write);
  and and_4 (and_4_out, write_register[0], write_register[1], not_11_out, not_12_out, write);
  and and_5 (and_5_out, not_13_out, not_14_out, write_register[2], not_15_out, write);
  and and_6 (and_6_out, write_register[0], not_16_out, write_register[2], not_17_out, write);
  and and_7 (and_7_out, not_18_out, write_register[1], write_register[2], not_19_out, write);
  and and_8 (and_8_out, write_register[0], write_register[1], write_register[2], not_20_out, write);
  and and_9 (and_9_out, not_21_out, not_22_out, not_23_out, write_register[3], write);
  and and_10 (and_10_out, write_register[0], not_24_out, not_25_out, write_register[3], write);
  and and_11 (and_11_out, not_26_out, write_register[1], not_27_out, write_register[3], write);
  and and_12 (and_12_out, write_register[0], write_register[1], not_28_out, write_register[3], write);
  and and_13 (and_13_out, not_29_out, not_30_out, write_register[2], write_register[3], write);
  and and_14 (and_14_out, write_register[0], not_31_out, write_register[2], write_register[3], write);
  and and_15 (and_15_out, not_32_out, write_register[1], write_register[2], write_register[3], write);
  and and_16 (and_16_out, write_register[0], write_register[1], write_register[2], write_register[3], write);
  Register #(.width(16)) register_1 (.D(\input ), .Q(register_1_q), .clk(and_1_out));  // open: en, clr
  Register #(.width(16)) register_2 (.D(\input ), .Q(register_2_q), .clk(and_2_out));  // open: en, clr
  Register #(.width(16)) register_3 (.D(\input ), .Q(register_3_q), .clk(and_3_out));  // open: en, clr
  Register #(.width(16)) register_4 (.D(\input ), .Q(register_4_q), .clk(and_4_out));  // open: en, clr
  Register #(.width(16)) register_5 (.D(\input ), .Q(register_5_q), .clk(and_5_out));  // open: en, clr
  Register #(.width(16)) register_6 (.D(\input ), .Q(register_6_q), .clk(and_6_out));  // open: en, clr
  Register #(.width(16)) register_7 (.D(\input ), .Q(register_7_q), .clk(and_7_out));  // open: en, clr
  Register #(.width(16)) register_8 (.D(\input ), .Q(register_8_q), .clk(and_8_out));  // open: en, clr
  Register #(.width(16)) register_9 (.D(\input ), .Q(register_9_q), .clk(and_9_out));  // open: en, clr
  Register #(.width(16)) register_10 (.D(\input ), .Q(register_10_q), .clk(and_10_out));  // open: en, clr
  Register #(.width(16)) register_11 (.D(\input ), .Q(register_11_q), .clk(and_11_out));  // open: en, clr
  Register #(.width(16)) register_12 (.D(\input ), .Q(register_12_q), .clk(and_12_out));  // open: en, clr
  Register #(.width(16)) register_13 (.D(\input ), .Q(register_13_q), .clk(and_13_out));  // open: en, clr
  Register #(.width(16)) register_14 (.D(\input ), .Q(register_14_q), .clk(and_14_out));  // open: en, clr
  Register #(.width(16)) register_15 (.D(\input ), .Q(register_15_q), .clk(and_15_out));  // open: en, clr
  Register #(.width(16)) register_16 (.D(\input ), .Q(register_16_q), .clk(and_16_out));  // open: en, clr
  Multiplexer #(.select(4), .width(16), .enable("false")) multiplexer_1 (
    .in0(register_1_q), .in1(register_2_q), .in2(register_3_q), .in3(register_4_q), .in4(register_5_q),
    .in5(register_6_q), .in6(register_7_q), .in7(register_8_q), .in8(register_9_q), .in9(register_10_q),
    .in10(register_11_q), .in11(register_12_q), .in12(register_13_q), .in13(register_14_q),
    .in14(register_15_q), .in15(register_16_q), .out(output_0), .sel(multiplexer_2_out));
  Multiplexer #(.width(4), .enable("false")) multiplexer_2 (
    .in0(read_register_0), .in1(write_register), .out(multiplexer_2_out), .sel(single_reg_instr));
  Multiplexer #(.select(4), .width(16), .enable("false")) multiplexer_3 (
    .in0(register_1_q), .in1(register_2_q), .in2(register_3_q), .in3(register_4_q), .in4(register_5_q),
    .in5(register_6_q), .in6(register_7_q), .in7(register_8_q), .in8(register_9_q), .in9(register_10_q),
    .in10(register_11_q), .in11(register_12_q), .in12(register_13_q), .in13(register_14_q),
    .in14(register_15_q), .in15(register_16_q), .out(output_1), .sel(read_register_1));

  // Other names for the same wires on the sheet: wr[3:0] = write_register
endmodule

module test (
  output [15:0] output_0,
  output [15:0] output_1
);

  wire and_1_out, buffer_1_out, buffer_2_out, buffer_3_out, buffer_4_out, buffer_5_out, buffer_6_out,
       buffer_7_out, buffer_8_out, clock_1_out;
  wire [1:0] counter_5_q;
  wire [3:0] counter_2_q, counter_3_q, counter_4_q;
  wire [15:0] counter_1_q;

  Clock clock_1 (.out(clock_1_out));
  Counter #(.width(16), .max('hffff)) counter_1 (
    .Q(counter_1_q), .clk(clock_1_out));  // open: load, D, count, carry, clr
  Counter #(.width(4), .max('hf)) counter_2 (.Q(counter_2_q), .clk(clock_1_out));  // open: load, D, count, carry, clr
  buf buffer_1 (buffer_1_out, clock_1_out);
  Counter #(.width(4), .max('hf)) counter_3 (.Q(counter_3_q), .clk(clock_1_out));  // open: load, D, count, carry, clr
  Counter #(.width(4), .max('hf)) counter_4 (.Q(counter_4_q), .clk(clock_1_out));  // open: load, D, count, carry, clr
  Counter #(.width(2), .max('h2)) counter_5 (.Q(counter_5_q), .clk(clock_1_out));  // open: load, D, count, carry, clr
  buf buffer_2 (buffer_2_out, buffer_5_out);
  buf buffer_3 (buffer_3_out, buffer_1_out);
  buf buffer_4 (buffer_4_out, buffer_2_out);
  buf buffer_5 (buffer_5_out, buffer_3_out);
  and and_1 (and_1_out, counter_5_q[1], buffer_7_out);
  buf buffer_6 (buffer_6_out, buffer_8_out);
  buf buffer_7 (buffer_7_out, buffer_6_out);
  buf buffer_8 (buffer_8_out, buffer_4_out);
  main main_1 (
    .\input (counter_1_q), .write_register(counter_2_q), .read_register_0(counter_3_q),
    .read_register_1(counter_4_q), .write(and_1_out), .output_0(output_0), .output_1(output_1));  // open: single_reg_instr
endmodule
