// Logisim project alu.circ as structural Verilog: 1 circuit, main circuit main
module main (
  input  [15:0] reg_1,
  input  [15:0] reg_2,
  input  [7:0] immediate,
  input  [3:0] opcode,
  output [15:0] \output 
);

  wire [15:0] adder_1_out, adder_2_out, adder_3_out, and_1_out, bit_extender_1_out, bit_extender_2_out,
       or_1_out, shifter_1_out, shifter_2_out;

  assign bit_extender_1_out = {{8{immediate[7]}}, immediate};  // Bit_Extender bit_extender_1
  assign bit_extender_2_out = {{8{1'b0}}, immediate};  // Bit_Extender bit_extender_2
  Adder #(.width(16)) adder_1 (.a(reg_1), .b(reg_2), .out(adder_1_out));  // open: cin, cout
  assign and_1_out = reg_1 & reg_2;  // AND_Gate and_1, 16 bits wide
  assign or_1_out = reg_1 | reg_2;  // OR_Gate or_1, 16 bits wide
  Shifter #(.width(16)) shifter_1 (.in(reg_1), .\dist (reg_2[3:0]), .out(shifter_1_out));
  Adder #(.width(16)) adder_2 (.a(reg_1), .b(bit_extender_1_out), .out(adder_2_out));  // open: cin, cout
  Adder #(.width(16)) adder_3 (.a(reg_1), .b(bit_extender_2_out), .out(adder_3_out));  // open: cin, cout
  Shifter #(.width(16)) shifter_2 (.in(reg_1), .\dist (immediate[3:0]), .out(shifter_2_out));
  Multiplexer #(.select(4), .width(16), .enable("false")) multiplexer_1 (
    .in8(adder_1_out), .in9(and_1_out), .in10(or_1_out), .in11(shifter_1_out), .in12(adder_2_out),
    .in13(adder_3_out), .in15(shifter_2_out), .out(\output ), .sel(opcode));  // open: in0, in1, in2, in3, in4, in5, in6, in7, in14
endmodule
