// Logisim project control.circ as structural Verilog: 1 circuit, main circuit main
module main (
  input  [3:0] opcode,
  input  clock,
  output write,
  output alu_source,
  output single_reg_instr,
  output store_memory
);

  wire and_1_out, and_2_out, and_3_out, buffer_1_out, buffer_2_out, buffer_3_out, buffer_4_out, buffer_5_out,
       buffer_6_out, buffer_7_out, buffer_8_out, buffer_9_out, buffer_10_out, buffer_11_out, buffer_12_out,
       buffer_13_out, buffer_14_out, buffer_15_out, buffer_16_out, buffer_17_out, buffer_18_out,
       buffer_19_out, buffer_20_out, buffer_21_out, buffer_22_out, buffer_23_out, buffer_24_out,
       buffer_25_out, buffer_26_out, buffer_27_out, buffer_28_out, buffer_29_out, buffer_30_out,
       buffer_31_out, buffer_32_out, buffer_33_out, buffer_34_out, buffer_35_out, buffer_36_out,
       buffer_37_out, buffer_38_out, buffer_39_out, buffer_40_out, buffer_41_out, buffer_42_out,
       buffer_43_out, buffer_44_out, buffer_45_out, buffer_46_out, buffer_47_out, buffer_48_out,
       buffer_49_out, buffer_50_out, buffer_51_out, buffer_52_out, buffer_53_out, buffer_54_out,
       buffer_55_out, buffer_56_out, buffer_57_out, buffer_58_out, buffer_59_out, buffer_60_out,
       buffer_61_out, buffer_62_out, buffer_63_out, buffer_64_out, buffer_66_out, buffer_67_out,
       buffer_68_out, buffer_69_out, buffer_70_out, buffer_71_out, buffer_72_out, buffer_73_out,
       buffer_74_out, buffer_75_out, buffer_76_out, buffer_77_out, buffer_78_out, buffer_79_out,
       buffer_80_out, buffer_81_out, buffer_82_out, buffer_83_out, buffer_84_out, buffer_85_out,
       buffer_86_out, buffer_88_out, buffer_89_out, buffer_90_out, buffer_91_out, buffer_92_out,
       buffer_93_out, buffer_94_out, buffer_95_out, buffer_96_out, buffer_97_out, buffer_98_out,
       buffer_99_out, buffer_100_out, buffer_101_out, buffer_102_out, buffer_103_out, buffer_104_out,
       buffer_105_out, buffer_106_out, buffer_107_out, buffer_108_out, buffer_109_out, not_1_out, not_2_out,
       not_3_out, not_4_out, not_5_out, or_1_out;

  buf buffer_1 (buffer_1_out, buffer_3_out);
  buf buffer_2 (buffer_2_out, buffer_1_out);
  buf buffer_3 (buffer_3_out, buffer_24_out);
  buf buffer_4 (buffer_4_out, buffer_5_out);
  buf buffer_5 (buffer_5_out, buffer_6_out);
  buf buffer_6 (buffer_6_out, clock);
  buf buffer_7 (buffer_7_out, buffer_9_out);
  buf buffer_8 (buffer_8_out, buffer_7_out);
  buf buffer_9 (buffer_9_out, buffer_10_out);
  buf buffer_10 (buffer_10_out, buffer_2_out);
  buf buffer_11 (buffer_11_out, buffer_12_out);
  buf buffer_12 (buffer_12_out, buffer_4_out);
  buf buffer_13 (buffer_13_out, buffer_11_out);
  buf buffer_14 (buffer_14_out, buffer_13_out);
  buf buffer_15 (buffer_15_out, buffer_8_out);
  buf buffer_16 (buffer_16_out, buffer_19_out);
  buf buffer_17 (buffer_17_out, buffer_14_out);
  buf buffer_18 (buffer_18_out, buffer_16_out);
  buf buffer_19 (buffer_19_out, buffer_17_out);
  not not_1 (not_1_out, opcode[0]);
  not not_2 (not_2_out, opcode[1]);
  not not_3 (not_3_out, opcode[3]);
  not not_4 (not_4_out, opcode[1]);
  not not_5 (not_5_out, opcode[3]);
  buf buffer_20 (buffer_20_out, buffer_21_out);
  buf buffer_21 (buffer_21_out, buffer_18_out);
  buf buffer_22 (buffer_22_out, buffer_20_out);
  buf buffer_23 (buffer_23_out, buffer_22_out);
  and and_1 (and_1_out, not_1_out, not_2_out, opcode[2], not_3_out);
  and and_2 (and_2_out, opcode[0], not_4_out, opcode[2], not_5_out);
  buf buffer_24 (buffer_24_out, buffer_23_out);
  or or_1 (or_1_out, and_1_out, opcode[3]);
  and and_3 (and_3_out, or_1_out, buffer_15_out);
  buf buffer_25 (buffer_25_out, buffer_26_out);
  buf buffer_26 (buffer_26_out, buffer_27_out);
  buf buffer_27 (buffer_27_out, buffer_106_out);
  buf buffer_28 (buffer_28_out, buffer_30_out);
  buf buffer_29 (buffer_29_out, buffer_28_out);
  buf buffer_30 (buffer_30_out, buffer_31_out);
  buf buffer_31 (buffer_31_out, buffer_107_out);
  buf buffer_32 (buffer_32_out, buffer_34_out);
  buf buffer_33 (buffer_33_out, buffer_108_out);
  buf buffer_34 (buffer_34_out, buffer_33_out);
  buf buffer_35 (buffer_35_out, buffer_36_out);
  buf buffer_36 (buffer_36_out, buffer_37_out);
  buf buffer_37 (buffer_37_out, buffer_109_out);
  buf buffer_38 (buffer_38_out, buffer_40_out);
  buf buffer_39 (buffer_39_out, buffer_38_out);
  buf buffer_40 (buffer_40_out, and_3_out);
  and and_4 (single_reg_instr, opcode[3], opcode[2]);
  buf buffer_41 (buffer_41_out, and_2_out);
  buf buffer_42 (buffer_42_out, buffer_43_out);
  buf buffer_43 (buffer_43_out, buffer_41_out);
  buf buffer_44 (buffer_44_out, buffer_25_out);
  buf buffer_45 (buffer_45_out, buffer_46_out);
  buf buffer_46 (buffer_46_out, buffer_44_out);
  buf buffer_47 (buffer_47_out, buffer_45_out);
  buf buffer_48 (buffer_48_out, buffer_51_out);
  buf buffer_49 (buffer_49_out, buffer_50_out);
  buf buffer_50 (buffer_50_out, buffer_48_out);
  buf buffer_51 (buffer_51_out, buffer_29_out);
  buf buffer_52 (buffer_52_out, buffer_32_out);
  buf buffer_53 (buffer_53_out, buffer_52_out);
  buf buffer_54 (buffer_54_out, buffer_55_out);
  buf buffer_55 (buffer_55_out, buffer_53_out);
  buf buffer_56 (buffer_56_out, buffer_59_out);
  buf buffer_57 (buffer_57_out, buffer_35_out);
  buf buffer_58 (buffer_58_out, buffer_56_out);
  buf buffer_59 (buffer_59_out, buffer_57_out);
  buf buffer_60 (buffer_60_out, buffer_39_out);
  buf buffer_61 (buffer_61_out, buffer_63_out);
  buf buffer_62 (buffer_62_out, buffer_60_out);
  buf buffer_63 (buffer_63_out, buffer_62_out);
  buf buffer_64 (buffer_64_out, buffer_66_out);
  buf buffer_65 (store_memory, buffer_64_out);
  buf buffer_66 (buffer_66_out, buffer_42_out);
  buf buffer_67 (buffer_67_out, buffer_68_out);
  buf buffer_68 (buffer_68_out, buffer_69_out);
  buf buffer_69 (buffer_69_out, buffer_47_out);
  buf buffer_70 (buffer_70_out, buffer_67_out);
  buf buffer_71 (buffer_71_out, buffer_74_out);
  buf buffer_72 (buffer_72_out, buffer_73_out);
  buf buffer_73 (buffer_73_out, buffer_49_out);
  buf buffer_74 (buffer_74_out, buffer_72_out);
  buf buffer_75 (buffer_75_out, buffer_54_out);
  buf buffer_76 (buffer_76_out, buffer_78_out);
  buf buffer_77 (buffer_77_out, buffer_75_out);
  buf buffer_78 (buffer_78_out, buffer_77_out);
  buf buffer_79 (buffer_79_out, buffer_58_out);
  buf buffer_80 (buffer_80_out, buffer_82_out);
  buf buffer_81 (buffer_81_out, buffer_80_out);
  buf buffer_82 (buffer_82_out, buffer_79_out);
  buf buffer_83 (buffer_83_out, buffer_86_out);
  buf buffer_84 (buffer_84_out, buffer_85_out);
  buf buffer_85 (buffer_85_out, buffer_83_out);
  buf buffer_86 (buffer_86_out, buffer_61_out);
  buf buffer_87 (write, buffer_88_out);
  buf buffer_88 (buffer_88_out, buffer_89_out);
  buf buffer_89 (buffer_89_out, buffer_70_out);
  buf buffer_90 (buffer_90_out, buffer_91_out);
  buf buffer_91 (buffer_91_out, buffer_92_out);
  buf buffer_92 (buffer_92_out, buffer_71_out);
  buf buffer_93 (buffer_93_out, buffer_90_out);
  buf buffer_94 (buffer_94_out, buffer_97_out);
  buf buffer_95 (buffer_95_out, buffer_96_out);
  buf buffer_96 (buffer_96_out, buffer_94_out);
  buf buffer_97 (buffer_97_out, buffer_76_out);
  buf buffer_98 (buffer_98_out, buffer_99_out);
  buf buffer_99 (buffer_99_out, buffer_100_out);
  buf buffer_100 (buffer_100_out, buffer_81_out);
  buf buffer_101 (buffer_101_out, buffer_98_out);
  buf buffer_102 (buffer_102_out, buffer_105_out);
  buf buffer_103 (buffer_103_out, buffer_84_out);
  buf buffer_104 (buffer_104_out, buffer_103_out);
  buf buffer_105 (buffer_105_out, buffer_104_out);
  buf buffer_106 (buffer_106_out, buffer_93_out);
  buf buffer_107 (buffer_107_out, buffer_95_out);
  buf buffer_108 (buffer_108_out, buffer_101_out);
  buf buffer_109 (buffer_109_out, buffer_102_out);

  assign alu_source = opcode[3];

  // Notes on the sheet:
  //   if previous opcode had write on, and current one needs it off, fast clock may still trigger write for the current opcode. We need to delay clock to prevent this
  //   16-bit alu add needs 49 cycle delays
  //   16-bit shifter needs 30 more than adder
endmodule
