// Logisim project proc.circ as structural Verilog: 1 circuit, main circuit main
module main (
);

  wire buffer_1_out, clock_out, control_alu_source, control_single_reg_instr, control_store_memory,
       control_write, not_1_out;
  wire [3:0] fetch_decode_jump_opcode, fetch_decode_jump_reg_0, fetch_decode_jump_reg_1,
       fetch_decode_jump_reg_2;
  wire [7:0] fetch_decode_jump_immediate;
  wire [11:0] fetch_decode_jump_address_input;
  wire [15:0] alu_output, multiplexer_1_out, ram_1_data, ram_2_data, reg_file_output_0, reg_file_output_1;

  Clock clock (.out(clock_out));
  RAM #(.addrWidth(12), .dataWidth(16), .bus("separate")) ram_1 (
    .addr(fetch_decode_jump_address_input), .data(ram_1_data));  // open: din, str, sel, clk, ld, clr
  fetch_decode_jump_main fetch_decode_jump (
    .address_input(fetch_decode_jump_address_input), .clock(clock_out), .instruction_output(ram_1_data),
    .zero_register(reg_file_output_1), .reg_0(fetch_decode_jump_reg_0), .reg_1(fetch_decode_jump_reg_1),
    .reg_2(fetch_decode_jump_reg_2), .immediate(fetch_decode_jump_immediate),
    .opcode(fetch_decode_jump_opcode));
  control_main control (
    .opcode(fetch_decode_jump_opcode), .clock(clock_out), .write(control_write),
    .alu_source(control_alu_source), .single_reg_instr(control_single_reg_instr),
    .store_memory(control_store_memory));
  Multiplexer #(.width(16), .enable("false")) multiplexer_1 (
    .in0(ram_2_data), .in1(alu_output), .out(multiplexer_1_out), .sel(control_alu_source));
  _16_reg_file_main reg_file (
    .\input (multiplexer_1_out), .write_register(fetch_decode_jump_reg_0),
    .read_register_0(fetch_decode_jump_reg_1), .read_register_1(fetch_decode_jump_reg_2),
    .write(control_write), .single_reg_instr(control_single_reg_instr), .output_0(reg_file_output_0),
    .output_1(reg_file_output_1));
  alu_main alu (
    .reg_1(reg_file_output_0), .reg_2(reg_file_output_1), .immediate(fetch_decode_jump_immediate),
    .opcode(fetch_decode_jump_opcode), .\output (alu_output));
  not not_1 (not_1_out, control_store_memory);
  buf buffer_1 (buffer_1_out, control_store_memory);
  RAM #(.addrWidth(16), .dataWidth(16), .bus("separate")) ram_2 (
    .addr(reg_file_output_0), .din(reg_file_output_1), .data(ram_2_data), .clk(buffer_1_out), .ld(not_1_out));  // open: str, sel, clr
endmodule
