// Logisim project Offline 1.circ as structural Verilog: 1 circuit, main circuit main
module main (
  input  cs1,
  input  cs2,
  input  cs0,
  input  A0,
  input  B0,
  input  A1,
  input  B1,
  input  A2,
  input  B2,
  input  A3,
  input  B3,
  output Z,
  output F0,
  output S,
  output F1,
  output V,
  output C,
  output F2,
  output F3,
  output Cout
);

  wire adder_1_cout, adder_2_cout, adder_3_cout, and_1_out, and_2_out, and_3_out, and_4_out, not_1_out,
       not_2_out, or_1_out, or_2_out, or_3_out, or_4_out, or_5_out, xor_1_out;

  xor xor_1 (xor_1_out, cs2, cs0);
  not not_1 (not_1_out, xor_1_out);
  not not_2 (not_2_out, cs0);
  or or_1 (or_1_out, not_1_out, B0);
  or or_2 (or_2_out, not_1_out, B1);
  or or_3 (or_3_out, not_1_out, B2);
  or or_4 (or_4_out, not_1_out, B3);
  and and_1 (and_1_out, cs1, not_2_out);
  Adder #(.width(1)) adder_1 (.a(A0), .b(or_1_out), .out(F0), .cin(and_1_out), .cout(adder_1_cout));
  Adder #(.width(1)) adder_2 (.a(A1), .b(or_2_out), .out(F1), .cin(and_2_out), .cout(adder_2_cout));
  Adder #(.width(1)) adder_3 (.a(A2), .b(or_3_out), .out(F2), .cin(and_3_out), .cout(adder_3_cout));
  Adder #(.width(1)) adder_4 (.a(A3), .b(or_4_out), .out(F3), .cin(and_4_out), .cout(C));
  and and_2 (and_2_out, adder_1_cout, not_2_out);
  and and_3 (and_3_out, adder_2_cout, not_2_out);
  and and_4 (and_4_out, adder_3_cout, not_2_out);
  or or_5 (or_5_out, F0, F1, F2, F3);
  not not_3 (Z, or_5_out);
  xor xor_2 (V, and_4_out, C);

  assign Cout = C;
  assign S = F3;

  // Notes on the sheet:
  //   C0
  //   C1
  //   C2
  //   C3
endmodule
