// Logisim project IEEE754_Adder.circ as structural Verilog: 6 circuits, main circuit main
module main (
  input  Sign_A,
  input  [15:0] Significant_A,
  input  Sign_B,
  input  [15:0] Significant_B,
  input  [3:0] Exponent_in,
  output Sign_of_A_B,
  output [15:0] A_B,
  output [3:0] Exponent_Out,
  output Exponent_Overflow
);

  IEEE_Adder ieee_adder_1 (
    .Sign_A(Sign_A), .Significant_A(Significant_A), .Sign_B(Sign_B), .Significant_B(Significant_B),
    .Exponent_in(Exponent_in), .A_B(A_B), .Exponent_Out(Exponent_Out), .Exponent_Overflow(Exponent_Overflow),
    .Sign_of_A_B(Sign_of_A_B));
endmodule

module Special_Adder (
  input  Sign_A,
  input  [15:0] A___A______B,
  input  Sign_B,
  input  [15:0] B,
  output Sign_Out,
  output [15:0] A_B,
  output Carry
);

  wire [15:0] adder_1_out, n2s_complement_1__2s_comp, n2s_complement_2__2s_comp;

  _2s_complement u_2s_complement_1 (.Input(A___A______B), .Control(Sign_A), ._2s_comp(n2s_complement_1__2s_comp));
  _2s_complement u_2s_complement_2 (.Input(B), .Control(Sign_B), ._2s_comp(n2s_complement_2__2s_comp));
  Adder #(.width(16)) adder_1 (
    .a(n2s_complement_1__2s_comp), .b(n2s_complement_2__2s_comp), .out(adder_1_out), .cin(1'b0), .cout(Carry));
  _2s_complement u_2s_complement_3 (.Input(adder_1_out), .Control(Sign_A), ._2s_comp(A_B));

  assign Sign_Out = Sign_A;
endmodule

module Significant_adder (
  input  Sign_A,
  input  [15:0] Significant_A,
  input  Sign_B,
  input  [15:0] Significant_B,
  output Sign,
  output [15:0] A_B,
  output Carry_out
);

  wire magnitude_comparator_1_sign_a_2, magnitude_comparator_1_sign_b_2;
  wire [15:0] magnitude_comparator_1_a___a____b, magnitude_comparator_1_b;

  Magnitude_Comparator magnitude_comparator_1 (
    .Sign_A(Sign_A), .Significant_A(Significant_A), .Sign_B(Sign_B), .Significant_B(Significant_B),
    .Sign_A_2(magnitude_comparator_1_sign_a_2), .A___A____B(magnitude_comparator_1_a___a____b),
    .Sign_B_2(magnitude_comparator_1_sign_b_2), .B(magnitude_comparator_1_b));
  Special_Adder special_adder_1 (
    .A___A______B(magnitude_comparator_1_a___a____b), .B(magnitude_comparator_1_b),
    .Sign_A(magnitude_comparator_1_sign_a_2), .Sign_B(magnitude_comparator_1_sign_b_2), .Sign_Out(Sign),
    .A_B(A_B), .Carry(Carry_out));
endmodule

module _2s_complement (
  input  Control,
  input  [15:0] Input,
  output [15:0] _2s_comp
);

  wire [15:0] xor_1_out;

  assign xor_1_out = {16{Control}} ^ Input;  // XOR_Gate xor_1, 16 bits wide
  Adder #(.width(16)) adder_1 (.a({16{1'b0}}), .b(xor_1_out), .out(_2s_comp), .cin(Control));  // open: cout
endmodule

module Magnitude_Comparator (
  input  Sign_A,
  input  [15:0] Significant_A,
  input  Sign_B,
  input  [15:0] Significant_B,
  output Sign_A_2,
  output [15:0] A___A____B,
  output Sign_B_2,
  output [15:0] B
);

  wire comparator_1_lt, not_1_out;

  Comparator #(.width(16), .mode("unsigned")) comparator_1 (
    .a(Significant_A), .b(Significant_B), .lt(comparator_1_lt));  // open: gt, eq
  not not_1 (not_1_out, comparator_1_lt);
  Multiplexer multiplexer_1 (.in0(Sign_A), .in1(Sign_B), .out(Sign_A_2), .sel(comparator_1_lt));  // open: en
  Multiplexer #(.width(16)) multiplexer_2 (
    .in0(Significant_A), .in1(Significant_B), .out(A___A____B), .sel(comparator_1_lt));  // open: en
  Multiplexer multiplexer_3 (.in0(Sign_A), .in1(Sign_B), .out(Sign_B_2), .sel(not_1_out));  // open: en
  Multiplexer #(.width(16)) multiplexer_4 (
    .in0(Significant_A), .in1(Significant_B), .out(B), .sel(not_1_out));  // open: en
endmodule

module IEEE_Adder (
  input  Sign_A,
  input  [15:0] Significant_A,
  input  Sign_B,
  input  [15:0] Significant_B,
  input  [3:0] Exponent_in,
  output Sign_of_A_B,
  output [15:0] A_B,
  output [3:0] Exponent_Out,
  output Exponent_Overflow
);

  wire significant_adder_1_carry_out;
  wire [3:0] bit_extender_1_out, bit_extender_2_out;
  wire [15:0] multiplexer_1_out, shifter_1_out, significant_adder_1_a_b;

  Significant_adder significant_adder_1 (
    .Sign_A(Sign_A), .Significant_A(Significant_A), .Sign_B(Sign_B), .Significant_B(Significant_B),
    .Sign(Sign_of_A_B), .A_B(significant_adder_1_a_b), .Carry_out(significant_adder_1_carry_out));
  assign bit_extender_1_out = {{3{1'b0}}, significant_adder_1_carry_out};  // Bit_Extender bit_extender_1
  assign bit_extender_2_out = {{3{1'b0}}, significant_adder_1_carry_out};  // Bit_Extender bit_extender_2
  Shifter #(.width(16), .shift("lr")) shifter_1 (
    .in(significant_adder_1_a_b), .\dist (bit_extender_1_out), .out(shifter_1_out));
  Multiplexer #(.width(16)) multiplexer_1 (
    .in0({16{1'b0}}), .in1(16'h8000), .out(multiplexer_1_out), .sel(significant_adder_1_carry_out));  // open: en
  Adder #(.width(16)) adder_1 (.a(shifter_1_out), .b(multiplexer_1_out), .out(A_B), .cin(1'b0));  // open: cout
  Adder #(.width(4)) adder_2 (
    .a(Exponent_in), .b(bit_extender_2_out), .out(Exponent_Out), .cin(1'b0), .cout(Exponent_Overflow));
endmodule
