// Logisim project 8_Bit_Register.circ as structural Verilog
module Register (
  input  [7:0] Write_Data,
  input  [2:0] Read_Select,
  input  [2:0] Write_Select,
  input  [7:0] Write_Data_2,
  input  [2:0] Read_Select_2,
  input  Write_Enable,
  output [7:0] Read_Data,
  output [7:0] Read_Data_2
);

  wire and_1_out, and_2_out, and_3_out, and_4_out, and_5_out, and_6_out, Clock_out, demultiplexer_1_out0,
       demultiplexer_1_out1, demultiplexer_1_out2, demultiplexer_1_out3, demultiplexer_1_out4,
       demultiplexer_1_out5;
  wire [7:0] T0_q, T1_q, T2_q, T3_q, T4_q, ZERO_q;

  Demultiplexer #(.select(3), .enable("false")) demultiplexer_1 (
    .out0(demultiplexer_1_out0), .out1(demultiplexer_1_out1), .out2(demultiplexer_1_out2),
    .out3(demultiplexer_1_out3), .out4(demultiplexer_1_out4), .out5(demultiplexer_1_out5), .sel(Write_Select));  // open: out6, out7, in
  Register_part ZERO (.D(Write_Data), .en(and_1_out), .clk(Clock_out), .Q(ZERO_q));  // open: clr
  and and_1 (and_1_out, demultiplexer_1_out0, Write_Enable);
  Register_part T0 (.D(Write_Data_2), .en(and_2_out), .clk(Clock_out), .Q(T0_q));  // open: clr
  and and_2 (and_2_out, demultiplexer_1_out1, Write_Enable);
  Clock Clock (.out(Clock_out));
  and and_3 (and_3_out, demultiplexer_1_out2, Write_Enable);
  and and_4 (and_4_out, demultiplexer_1_out3, Write_Enable);
  Register_part T1 (.D(Write_Data_2), .en(and_3_out), .clk(Clock_out), .Q(T1_q));  // open: clr
  Register_part T2 (.D(Write_Data_2), .en(and_4_out), .clk(Clock_out), .Q(T2_q));  // open: clr
  and and_5 (and_5_out, demultiplexer_1_out4, Write_Enable);
  and and_6 (and_6_out, demultiplexer_1_out5, Write_Enable);
  Register_part T3 (.D(Write_Data_2), .en(and_5_out), .clk(Clock_out), .Q(T3_q));  // open: clr
  Register_part T4 (.D(Write_Data_2), .en(and_6_out), .clk(Clock_out), .Q(T4_q));  // open: clr
  Multiplexer #(.select(3), .width(8), .enable("false")) multiplexer_1 (
    .in0(ZERO_q), .in1(T0_q), .in2(T1_q), .in3(T2_q), .in4(T3_q), .in5(T4_q), .out(Read_Data),
    .sel(Read_Select));  // open: in6, in7
  Multiplexer #(.select(3), .width(8), .enable("false")) multiplexer_2 (
    .in0(ZERO_q), .in1(T0_q), .in2(T1_q), .in3(T2_q), .in4(T3_q), .in5(T4_q), .out(Read_Data_2),
    .sel(Read_Select_2));  // open: in6, in7
endmodule
