// Logisim project ALU_1.circ as structural Verilog: 2 circuits, main circuit main
module main (
  input  [2:0] ALUOpcode,
  input  [7:0] in_2,
  input  [7:0] in_3,
  output [7:0] out_4,
  output out_5
);

  wire or_1_out;
  wire [1:0] or_3_out;
  wire [7:0] adder_1_out, adder_2_out, and_2_out, bit_extender_1_out, bit_extender_2_out, or_2_out, or_4_out,
       sll_srl_sra_1_out_4, xor_1_out, xor_2_out;

  or or_1 (or_1_out, ALUOpcode[0], ALUOpcode[1]);
  assign bit_extender_1_out = {{7{ALUOpcode[0]}}, ALUOpcode[0]};  // Bit_Extender bit_extender_1
  assign xor_1_out = bit_extender_1_out ^ in_3;  // XOR_Gate xor_1, 8 bits wide
  assign or_2_out = in_2 | in_3;  // OR_Gate or_2, 8 bits wide
  assign xor_2_out = in_3 ^ in_2;  // XOR_Gate xor_2, 8 bits wide
  or or_3 (or_3_out[0], ALUOpcode[2], ALUOpcode[1]);
  and and_1 (or_3_out[1], ALUOpcode[2], or_1_out);
  assign and_2_out = bit_extender_1_out & xor_2_out;  // AND_Gate and_2, 8 bits wide
  assign bit_extender_2_out = {{7{ALUOpcode[2]}}, ALUOpcode[2]};  // Bit_Extender bit_extender_2
  Adder adder_1 (.a(in_2), .b(xor_1_out), .out(adder_1_out), .cin(ALUOpcode[0]), .cout(out_5));
  assign or_4_out = and_2_out | bit_extender_2_out;  // OR_Gate or_4, 8 bits wide
  Adder #(.width(1)) adder_2 (.a(or_2_out[0]), .b(or_4_out[0]), .out(adder_2_out[0]));  // open: cin, cout
  Adder #(.width(1)) adder_3 (.a(or_2_out[1]), .b(or_4_out[1]), .out(adder_2_out[1]));  // open: cin, cout
  Adder #(.width(1)) adder_4 (.a(or_2_out[2]), .b(or_4_out[2]), .out(adder_2_out[2]));  // open: cin, cout
  Adder #(.width(1)) adder_5 (.a(or_2_out[3]), .b(or_4_out[3]), .out(adder_2_out[3]));  // open: cin, cout
  Adder #(.width(1)) adder_6 (.a(or_2_out[4]), .b(or_4_out[4]), .out(adder_2_out[4]));  // open: cin, cout
  Adder #(.width(1)) adder_7 (.a(or_2_out[5]), .b(or_4_out[5]), .out(adder_2_out[5]));  // open: cin, cout
  Adder #(.width(1)) adder_8 (.a(or_2_out[6]), .b(or_4_out[6]), .out(adder_2_out[6]));  // open: cin, cout
  Adder #(.width(1)) adder_9 (.a(or_2_out[7]), .b(or_4_out[7]), .out(adder_2_out[7]));  // open: cin, cout
  sll_srl_sra sll_srl_sra_1 (.in_1(in_3), .in_2(in_2), .in_3(ALUOpcode[1:0]), .out_4(sll_srl_sra_1_out_4));
  Multiplexer #(.enable("false"), .select(2), .width(8)) multiplexer_1 (
    .in0(adder_1_out), .in1(adder_2_out), .in3(sll_srl_sra_1_out_4), .out(out_4), .sel(or_3_out));  // open: in2

  // Notes on the sheet:
  //   A
  //   B
endmodule

module sll_srl_sra (
  input  [7:0] in_1,
  input  [7:0] in_2,
  input  [1:0] in_3,
  output [7:0] out_4
);

  wire and_1_out, comparator_1_lt, comparator_2_eq, comparator_2_gt, or_1_out;
  wire [7:0] multiplexer_1_out, multiplexer_3_out, shifter_1_out, shifter_2_out, shifter_3_out;

  Comparator comparator_1 (.a(in_2), .b({8{1'b0}}), .lt(comparator_1_lt));  // open: gt, eq
  Comparator comparator_2 (.a(in_2), .b(8'h8), .gt(comparator_2_gt), .eq(comparator_2_eq));  // open: lt
  or or_1 (or_1_out, comparator_2_eq, comparator_1_lt, comparator_2_gt);
  and and_1 (and_1_out, in_1[7], or_1_out, in_3[1], in_3[0], in_3[0]);
  Shifter shifter_1 (.in(in_1), .\dist (in_2[2:0]), .out(shifter_1_out));
  Shifter #(.shift("lr")) shifter_2 (.in(in_1), .\dist (in_2[2:0]), .out(shifter_2_out));
  Shifter #(.shift("ar")) shifter_3 (.in(in_1), .\dist (in_2[2:0]), .out(shifter_3_out));
  Multiplexer #(.enable("false"), .select(2), .width(8)) multiplexer_1 (
    .in1(shifter_1_out), .in2(shifter_2_out), .in3(shifter_3_out), .out(multiplexer_1_out), .sel(in_3));  // open: in0
  Multiplexer #(.enable("false"), .width(8)) multiplexer_2 (
    .in0(multiplexer_1_out), .in1(multiplexer_3_out), .out(out_4), .sel(or_1_out));
  Multiplexer #(.enable("false"), .width(8)) multiplexer_3 (
    .in0({8{1'b0}}), .in1({8{1'b1}}), .out(multiplexer_3_out), .sel(and_1_out));

  // Notes on the sheet:
  //   B
  //   A
  //   ALUOpcode
endmodule
