// Logisim project MIPS.circ as structural Verilog: 13 circuits, main circuit MIPS_8_BIT
module main (
  input  Reset
);

  wire CLK_out;

  Clock CLK (.out(CLK_out));
  MIPS_8_BIT mips_8_bit_1 (.CLK(CLK_out), .ResetPC(Reset));
  PipeLined_main pipelined_main_1 (.CLK(CLK_out), .ResetPC(Reset));
endmodule

module MIPS_8_BIT (
  input  CLK,
  input  ResetPC
);

  wire alu_1_zero, and_1_out, and_2_out, control_unit_1_alusrc, control_unit_1_beq, control_unit_1_bneq,
       control_unit_1_jmp, control_unit_1_memread, control_unit_1_memtoreg, control_unit_1_memwrite,
       control_unit_1_regdest, control_unit_1_regwrite, control_unit_1_shift, not_1_out, or_1_out;
  wire [2:0] control_unit_1_aluop;
  wire [3:0] multiplexer_1_out;
  wire [7:0] alu_1_aluout, bit_extender_1_out, datamemory_1_readdata, instructionmem_1_out_2_2,
       multiplexer_2_out, multiplexer_3_out, multiplexer_6_out, registermem_1_rval1, registermem_1_rval2;
  wire [11:0] adder_1_out, adder_2_out, bit_extender_2_out, multiplexer_4_out, multiplexer_5_out, PC_q;
  wire [19:0] instructionmem_1_out_2;

  Register #(.width(12)) PC (.D(multiplexer_5_out), .en(1'b1), .clk(CLK), .Q(PC_q), .clr(ResetPC));
  Adder #(.width(12)) adder_1 (.a(PC_q), .b(12'h1), .out(adder_1_out));  // open: cin, cout
  InstructionMem instructionmem_1 (
    .in_1(PC_q),
    .out_2({instructionmem_1_out_2[19:16], instructionmem_1_out_2_2, instructionmem_1_out_2[7:0]}));
  Multiplexer #(.enable("false"), .width(4)) multiplexer_1 (
    .in0(instructionmem_1_out_2_2[3:0]), .in1(instructionmem_1_out_2[7:4]), .out(multiplexer_1_out),
    .sel(control_unit_1_regdest));
  assign bit_extender_1_out = {{4{instructionmem_1_out_2[3]}}, instructionmem_1_out_2[3:0]};  // Bit_Extender bit_extender_1
  Control_Unit control_unit_1 (
    .Opcode(instructionmem_1_out_2[19:16]), .ALUop(control_unit_1_aluop), .jmp(control_unit_1_jmp),
    .bneq(control_unit_1_bneq), .beq(control_unit_1_beq), .ALUsrc(control_unit_1_alusrc),
    .RegDest(control_unit_1_regdest), .MemToReg(control_unit_1_memtoreg), .MemRead(control_unit_1_memread),
    .MemWrite(control_unit_1_memwrite), .RegWrite(control_unit_1_regwrite), .Shift(control_unit_1_shift));
  RegisterMem registermem_1 (
    .regWrite(control_unit_1_regwrite), .rreg1(instructionmem_1_out_2_2[7:4]),
    .rreg2(instructionmem_1_out_2_2[3:0]), .wreg(multiplexer_1_out), .wval(multiplexer_6_out), .CLK(CLK),
    .Reset(ResetPC), .rval1(registermem_1_rval1), .rval2(registermem_1_rval2));
  Multiplexer #(.enable("false"), .width(8)) multiplexer_2 (
    .in0(registermem_1_rval1), .in1(bit_extender_1_out), .out(multiplexer_2_out), .sel(control_unit_1_shift));
  Multiplexer #(.enable("false"), .width(8)) multiplexer_3 (
    .in0(registermem_1_rval2), .in1(instructionmem_1_out_2[7:0]), .out(multiplexer_3_out),
    .sel(control_unit_1_alusrc));
  assign bit_extender_2_out = {{4{instructionmem_1_out_2[7]}}, instructionmem_1_out_2[7:0]};  // Bit_Extender bit_extender_2
  Adder #(.width(12)) adder_2 (.a(adder_1_out), .b(bit_extender_2_out), .out(adder_2_out));  // open: cin, cout
  not not_1 (not_1_out, alu_1_zero);
  ALU alu_1 (
    .ALUop(control_unit_1_aluop), .A(multiplexer_2_out), .B(multiplexer_3_out), .Zero(alu_1_zero),
    .ALUOUT(alu_1_aluout));
  and and_1 (and_1_out, not_1_out, control_unit_1_bneq);
  and and_2 (and_2_out, control_unit_1_beq, alu_1_zero);
  Multiplexer #(.enable("false"), .width(12)) multiplexer_4 (
    .in0(adder_1_out), .in1(adder_2_out), .out(multiplexer_4_out), .sel(or_1_out));
  or or_1 (or_1_out, and_1_out, and_2_out);
  Multiplexer #(.enable("false"), .width(12)) multiplexer_5 (
    .in0(multiplexer_4_out), .in1({adder_1_out[11:8], instructionmem_1_out_2_2}), .out(multiplexer_5_out),
    .sel(control_unit_1_jmp));
  DataMemory datamemory_1 (
    .MemoryAddress(alu_1_aluout), .MemWrite(control_unit_1_memwrite), .MemRead(control_unit_1_memread),
    .CLK(CLK), .WriteData(registermem_1_rval2), .ReadData(datamemory_1_readdata));
  Multiplexer #(.enable("false"), .width(8)) multiplexer_6 (
    .in0(alu_1_aluout), .in1(datamemory_1_readdata), .out(multiplexer_6_out), .sel(control_unit_1_memtoreg));
endmodule

module Control_Unit (
  input  [3:0] Opcode,
  output [2:0] ALUop,
  output jmp,
  output bneq,
  output beq,
  output ALUsrc,
  output RegDest,
  output MemToReg,
  output MemRead,
  output MemWrite,
  output RegWrite,
  output Shift
);

  ROM #(.addrWidth(4), .dataWidth(13)) rom_1 (
    .addr(Opcode),
    .data({Shift, RegWrite, MemWrite, MemRead, MemToReg, RegDest, ALUsrc, beq, bneq, jmp, ALUop}));

  // Notes on the sheet:
  //   contents of rom_1 (hex, n*v repeats v):
  //   b40 1885 881 842 840 841 843 440 11 880 882 1886 884 f 21 883
endmodule

// t7
module RegisterMem (
  input  regWrite,
  input  [3:0] rreg1,
  input  [3:0] rreg2,
  input  [3:0] wreg,
  input  [7:0] wval,
  input  CLK,
  input  Reset,
  output [7:0] rval1,
  output [7:0] rval2
);

  wire demultiplexer_1_out0, demultiplexer_1_out1, demultiplexer_1_out2, demultiplexer_1_out3,
       demultiplexer_1_out4, demultiplexer_1_out5, demultiplexer_1_out6, demultiplexer_1_out7;
  wire [7:0] SP_q, t0_q, t1_q, t2_q, t3_q, t4_q, t6_q, zero_q;

  Demultiplexer #(.enable("false"), .select(4)) demultiplexer_1 (
    .out0(demultiplexer_1_out0), .out1(demultiplexer_1_out1), .out2(demultiplexer_1_out2),
    .out3(demultiplexer_1_out3), .out4(demultiplexer_1_out4), .out5(demultiplexer_1_out5),
    .out6(demultiplexer_1_out6), .out7(demultiplexer_1_out7), .in(regWrite), .sel(wreg));  // open: out8, out9, out10, out11, out12, out13, out14, out15
  Register t0 (.D(wval), .en(demultiplexer_1_out0), .clk(CLK), .Q(t0_q), .clr(Reset));
  Register t1 (.D(wval), .en(demultiplexer_1_out1), .clk(CLK), .Q(t1_q), .clr(Reset));
  Register t2 (.D(wval), .en(demultiplexer_1_out2), .clk(CLK), .Q(t2_q), .clr(Reset));
  Register t3 (.D(wval), .en(demultiplexer_1_out3), .clk(CLK), .Q(t3_q), .clr(Reset));
  Register t4 (.D(wval), .en(demultiplexer_1_out4), .clk(CLK), .Q(t4_q), .clr(Reset));
  Register zero (.D({8{1'b0}}), .en(demultiplexer_1_out5), .clk(CLK), .Q(zero_q), .clr(Reset));
  Register SP (.D(wval), .en(demultiplexer_1_out6), .clk(CLK), .Q(SP_q), .clr(Reset));
  Register t6 (.D(wval), .en(demultiplexer_1_out7), .clk(CLK), .Q(t6_q), .clr(Reset));
  Multiplexer #(.enable("false"), .select(4), .width(8)) multiplexer_1 (
    .in0(t0_q), .in1(t1_q), .in2(t2_q), .in3(t3_q), .in4(t4_q), .in5(zero_q), .in6(SP_q), .in7(t6_q),
    .out(rval1), .sel(rreg1));  // open: in8, in9, in10, in11, in12, in13, in14, in15
  Multiplexer #(.enable("false"), .select(4), .width(8)) multiplexer_2 (
    .in0(t0_q), .in1(t1_q), .in2(t2_q), .in3(t3_q), .in4(t4_q), .in5(zero_q), .in6(SP_q), .in7(t6_q),
    .out(rval2), .sel(rreg2));  // open: in8, in9, in10, in11, in12, in13, in14, in15
endmodule

module DataMemory (
  input  [7:0] MemoryAddress,
  input  MemWrite,
  input  MemRead,
  input  CLK,
  input  [7:0] WriteData,
  output [7:0] ReadData
);

  RAM #(.asyncread("true")) ram_1 (
    .addr(MemoryAddress), .we(MemWrite), .oe(MemRead), .clk(CLK), .din(WriteData), .dout(ReadData));
endmodule

module InstructionMem (
  input  [11:0] in_1,
  output [19:0] out_2
);

  ROM #(.addrWidth(12), .dataWidth(20)) rom_1 (.addr(in_1), .data(out_2));

  // Notes on the sheet:
  //   contents of rom_1 (hex, n*v repeats v):
  //   90010 90220 92330 92430 93100
endmodule

module ALU (
  input  [2:0] ALUop,
  input  [7:0] A,
  input  [7:0] B,
  output Zero,
  output [7:0] ALUOUT
);

  wire [7:0] adder_1_out, and_1_out, nor_1_out, or_1_out, shifter_1_out, shifter_2_out, subtractor_1_out;

  Adder adder_1 (.a(A), .b(B), .out(adder_1_out));  // open: cin, cout
  Subtractor subtractor_1 (.a(A), .b(B), .out(subtractor_1_out));  // open: bin, bout
  assign and_1_out = A & B;  // AND_Gate and_1, 8 bits wide
  assign or_1_out = A | B;  // OR_Gate or_1, 8 bits wide
  assign nor_1_out = ~(A | B);  // NOR_Gate nor_1, 8 bits wide
  Shifter shifter_1 (.in(B), .\dist (A[2:0]), .out(shifter_1_out));
  Shifter #(.shift("lr")) shifter_2 (.in(B), .\dist (A[2:0]), .out(shifter_2_out));
  Multiplexer #(.enable("false"), .select(3), .width(8)) multiplexer_1 (
    .in0(adder_1_out), .in1(subtractor_1_out), .in2(or_1_out), .in3(and_1_out), .in4(nor_1_out),
    .in5(shifter_1_out), .in6(shifter_2_out), .out(ALUOUT), .sel(ALUop));  // open: in7
  Comparator comparator_1 (.a({8{1'b0}}), .b(ALUOUT), .eq(Zero));  // open: gt, lt
endmodule

module ID_EX_REGISTER (
  input  ENABLE,
  input  CLK,
  input  RESET,
  input  [3:0] REG_ONE_READ_P,
  input  [7:0] REG_ONE_VAL_P,
  input  [3:0] REG_TWO_READ_P,
  input  [7:0] REG_TWO_VAL_P,
  input  [3:0] REG_WRITE_ADDRESS_P,
  input  [7:0] REG_WRITE_VAL_P,
  input  [7:0] SIGN_EXTEND_P,
  input  [2:0] ALU_OP_P,
  input  [7:0] ALU_A_P,
  input  [7:0] ALU_B_P,
  input  ALU_SRC_P,
  input  REG_DES_P,
  input  MEM_TO_REG_P,
  input  MEM_READ_P,
  input  MEM_WRITE_P,
  input  REG_WRITE_P,
  input  SHIFT_P,
  input  in_21,
  output [3:0] REG_ONE_READ_P2,
  output [7:0] REG_ONE_VAL_P2,
  output [3:0] REG_TWO_READ_P2,
  output [7:0] REG_TWO_VAL_P2,
  output [3:0] REG_WRITE_ADDRESS_P2,
  output [7:0] REG_WRITE_VAL_P2,
  output [7:0] SIGN_EXTEND_P2,
  output [2:0] ALU_OP_P2,
  output [7:0] ALU_A_P2,
  output [7:0] ALU_B_P2,
  output ALU_SRC_P2,
  output REG_DES_P2,
  output MEM_TO_REG_P2,
  output MEM_READ_P2,
  output MEM_WRITE_P2,
  output REG_WRITE_P2,
  output SHIFT_P2,
  output out_39
);

  Register #(.width(4)) REG_ONE_READ (.D(REG_ONE_READ_P), .en(ENABLE), .clk(CLK), .Q(REG_ONE_READ_P2), .clr(RESET));
  Register REG_TWO_READ (.D(REG_ONE_VAL_P), .en(ENABLE), .clk(CLK), .Q(REG_ONE_VAL_P2), .clr(RESET));
  Register #(.width(4)) REG_ONE_VAL (.D(REG_TWO_READ_P), .en(ENABLE), .clk(CLK), .Q(REG_TWO_READ_P2), .clr(RESET));
  Register REG_TWO_VAL (.D(REG_TWO_VAL_P), .en(ENABLE), .clk(CLK), .Q(REG_TWO_VAL_P2), .clr(RESET));
  Register #(.width(4)) REG_WRITE_ADDRESS (
    .D(REG_WRITE_ADDRESS_P), .en(ENABLE), .clk(CLK), .Q(REG_WRITE_ADDRESS_P2), .clr(RESET));
  Register REG_WRITE_VAL (.D(REG_WRITE_VAL_P), .en(ENABLE), .clk(CLK), .Q(REG_WRITE_VAL_P2), .clr(RESET));
  Register SIGN_EXTEND (.D(SIGN_EXTEND_P), .en(ENABLE), .clk(CLK), .Q(SIGN_EXTEND_P2), .clr(RESET));
  Register #(.width(3)) ALU_OP (.D(ALU_OP_P), .en(ENABLE), .clk(CLK), .Q(ALU_OP_P2), .clr(RESET));
  Register ALU_A (.D(ALU_A_P), .en(ENABLE), .clk(CLK), .Q(ALU_A_P2), .clr(RESET));
  Register ALU_B (.D(ALU_B_P), .en(ENABLE), .clk(CLK), .Q(ALU_B_P2), .clr(RESET));
  Register #(.width(1)) ALU_SRC (.D(ALU_SRC_P), .en(ENABLE), .clk(CLK), .Q(ALU_SRC_P2), .clr(RESET));
  Register #(.width(1)) REG_DES (.D(REG_DES_P), .en(ENABLE), .clk(CLK), .Q(REG_DES_P2), .clr(RESET));
  Register #(.width(1)) MEM_TO_REG (.D(MEM_TO_REG_P), .en(ENABLE), .clk(CLK), .Q(MEM_TO_REG_P2), .clr(RESET));
  Register #(.width(1)) MEM_READ (.D(MEM_READ_P), .en(ENABLE), .clk(CLK), .Q(MEM_READ_P2), .clr(RESET));
  Register #(.width(1)) MEM_WRITE (.D(MEM_WRITE_P), .en(ENABLE), .clk(CLK), .Q(MEM_WRITE_P2), .clr(RESET));
  Register #(.width(1)) REG_WRITE (.D(REG_WRITE_P), .en(ENABLE), .clk(CLK), .Q(REG_WRITE_P2), .clr(RESET));
  Register #(.width(1)) SHIFT (.D(SHIFT_P), .en(ENABLE), .clk(CLK), .Q(SHIFT_P2), .clr(RESET));
  Register #(.width(1)) register_1 (.D(in_21), .en(ENABLE), .clk(CLK), .Q(out_39), .clr(RESET));
endmodule

module Ex_mem (
  input  MemToReg,
  input  MemRead,
  input  MemWrite,
  input  RegWrite,
  input  ZeroFlag,
  input  [7:0] ALU_result,
  input  [3:0] WriteReg,
  input  CLK,
  input  Reset,
  output MemtoReg_out,
  output MemRead_out,
  output MemWrite_out,
  output RegWrite_out,
  output ZeroFlag_out,
  output [7:0] ALU_result_out,
  output [3:0] Write_reg_out
);

  Register #(.width(1)) register_1 (.D(MemToReg), .en(1'b1), .clk(CLK), .Q(MemtoReg_out), .clr(Reset));
  Register #(.width(1)) register_2 (.D(MemRead), .en(1'b1), .clk(CLK), .Q(MemRead_out), .clr(Reset));
  Register #(.width(1)) register_3 (.D(MemWrite), .en(1'b1), .clk(CLK), .Q(MemWrite_out), .clr(Reset));
  Register #(.width(1)) register_4 (.D(RegWrite), .en(1'b1), .clk(CLK), .Q(RegWrite_out), .clr(Reset));
  Register #(.width(1)) register_5 (.D(ZeroFlag), .en(1'b1), .clk(CLK), .Q(ZeroFlag_out), .clr(Reset));
  Register register_6 (.D(ALU_result), .en(1'b1), .clk(CLK), .Q(ALU_result_out), .clr(Reset));
  Register #(.width(4)) register_7 (.D(WriteReg), .en(1'b1), .clk(CLK), .Q(Write_reg_out), .clr(Reset));
endmodule

module Forwarding_Unit (
  input  EX_MEM_Reg_Write,
  input  MEM_WB_Reg_Write,
  input  [3:0] EX_MEM_RD,
  input  [3:0] MEM_WB_RD,
  input  [3:0] ID_EX_A,
  input  [3:0] ID_EX_B,
  output [1:0] Forward_A,
  output [1:0] Forward_B
);

  wire and_3_out, and_4_out, comparator_1_eq, comparator_2_eq, comparator_3_eq, comparator_4_eq,
       comparator_5_eq, comparator_6_eq, not_1_out, not_2_out, not_3_out, not_4_out;

  not not_1 (not_1_out, comparator_1_eq);
  Comparator #(.width(4)) comparator_1 (.a(ID_EX_A), .b(4'b0101), .eq(comparator_1_eq));  // open: gt, lt
  not not_2 (not_2_out, comparator_2_eq);
  Comparator #(.width(4)) comparator_2 (.a(ID_EX_B), .b(4'b0101), .eq(comparator_2_eq));  // open: gt, lt
  Comparator #(.width(4)) comparator_3 (.a(ID_EX_A), .b(EX_MEM_RD), .eq(comparator_3_eq));  // open: gt, lt
  Comparator #(.width(4)) comparator_4 (.a(ID_EX_B), .b(EX_MEM_RD), .eq(comparator_4_eq));  // open: gt, lt
  Comparator #(.width(4)) comparator_5 (.a(ID_EX_A), .b(MEM_WB_RD), .eq(comparator_5_eq));  // open: gt, lt
  Comparator #(.width(4)) comparator_6 (.a(ID_EX_B), .b(MEM_WB_RD), .eq(comparator_6_eq));  // open: gt, lt
  and and_1 (Forward_A[1], EX_MEM_Reg_Write, not_1_out, comparator_3_eq);
  and and_2 (Forward_B[1], EX_MEM_Reg_Write, not_2_out, comparator_4_eq);
  and and_3 (and_3_out, MEM_WB_Reg_Write, not_1_out, comparator_5_eq);
  and and_4 (and_4_out, MEM_WB_Reg_Write, not_2_out, comparator_6_eq);
  not not_3 (not_3_out, Forward_A[1]);
  not not_4 (not_4_out, Forward_B[1]);
  and and_5 (Forward_A[0], not_3_out, and_3_out);
  and and_6 (Forward_B[0], not_4_out, and_4_out);
endmodule

module IF_ID (
  input  [11:0] PCIN,
  input  [19:0] InstructionIN,
  input  Clk,
  input  Reset,
  output [11:0] PCOUT,
  output [19:0] InstructionOUT
);

  Register #(.width(32)) register_1 (
    .D({InstructionIN, PCIN}), .en(1'b1), .clk(Clk), .Q({InstructionOUT, PCOUT}), .clr(Reset));
endmodule

module MEM_WB (
  input  R_write_in,
  input  CLK,
  input  [3:0] WB_REG_IN,
  input  [7:0] MEM_DATA_IN,
  input  [7:0] ALU_RESULT_IN,
  input  [7:0] WRITE_DATA_IN,
  input  Mem2RegIn,
  input  RESET,
  output R_write_out,
  output [3:0] WB_REG_OUT,
  output [7:0] MEM_DATA_OUT,
  output [7:0] ALU_RESULT_OUT,
  output [7:0] WRITE_DATA_OUT,
  output Mem2RegOut,
  output CLK_WRITE
);

  Register #(.width(1)) register_1 (.D(R_write_in), .en(1'b1), .clk(CLK), .Q(R_write_out), .clr(RESET));
  Register #(.width(4)) register_2 (.D(WB_REG_IN), .en(1'b1), .clk(CLK), .Q(WB_REG_OUT), .clr(RESET));
  Register register_3 (.D(MEM_DATA_IN), .en(1'b1), .clk(CLK), .Q(MEM_DATA_OUT), .clr(RESET));
  Register register_4 (.D(ALU_RESULT_IN), .en(1'b1), .clk(CLK), .Q(ALU_RESULT_OUT), .clr(RESET));
  Register register_5 (.D(WRITE_DATA_IN), .en(1'b1), .clk(CLK), .Q(WRITE_DATA_OUT), .clr(RESET));
  Register #(.width(1)) register_6 (.D(Mem2RegIn), .en(1'b1), .clk(CLK), .Q(Mem2RegOut), .clr(RESET));
  Register #(.width(1)) register_7 (.D(R_write_in), .en(1'b1), .clk(CLK), .Q(CLK_WRITE), .clr(RESET));
endmodule

module PipeLined_main (
  input  CLK,
  input  ResetPC
);

  wire alu_1_zero, and_1_out, and_2_out, control_unit_1_alusrc, control_unit_1_memread,
       control_unit_1_memtoreg, control_unit_1_memwrite, control_unit_1_regdest, control_unit_1_regwrite,
       control_unit_1_shift, ex_mem_1_memread_out, ex_mem_1_memtoreg_out, ex_mem_1_memwrite_out,
       ex_mem_1_regwrite_out, id_ex_register_1_mem_read_p2, id_ex_register_1_mem_to_reg_p2,
       id_ex_register_1_mem_write_p2, id_ex_register_1_reg_write_p2, mem_wb_1_clk_write,
       mem_wb_1_r_write_out, not_1_out, or_1_out, undriven_2;
  wire [1:0] forwarding_unit_1_forward_a, forwarding_unit_1_forward_b;
  wire [2:0] control_unit_1_aluop, id_ex_register_1_alu_op_p2;
  wire [3:0] adder_1_out_2, ex_mem_1_write_reg_out, id_ex_register_1_reg_one_read_p2,
       id_ex_register_1_reg_two_read_p2, id_ex_register_1_reg_write_address_p2, mem_wb_1_wb_reg_out,
       multiplexer_1_out;
  wire [7:0] adder_1_out, alu_1_aluout, bit_extender_1_out, datamemory_1_readdata, ex_mem_1_alu_result_out,
       id_ex_register_1_reg_one_val_p2, id_ex_register_1_reg_two_val_p2, mem_wb_1_write_data_out,
       multiplexer_2_out, multiplexer_3_out, multiplexer_4_out, multiplexer_5_out, multiplexer_8_out,
       registermem_1_rval1, registermem_1_rval2, undriven;
  wire [11:0] adder_2_out, bit_extender_2_out, if_id_1_pcout, multiplexer_6_out, multiplexer_7_out, PC_q;
  wire [19:0] if_id_1_instructionout, instructionmem_1_out_2;

  Register #(.width(12)) PC (.D({adder_1_out_2, adder_1_out}), .en(1'b1), .clk(CLK), .Q(PC_q), .clr(ResetPC));
  InstructionMem instructionmem_1 (.in_1(PC_q), .out_2(instructionmem_1_out_2));
  IF_ID if_id_1 (
    .InstructionIN(instructionmem_1_out_2), .Clk(CLK), .Reset(ResetPC), .PCOUT(if_id_1_pcout),
    .InstructionOUT(if_id_1_instructionout));  // open: PCIN
  Adder #(.width(12)) adder_1 (.a(PC_q), .b(12'h1), .out({adder_1_out_2, adder_1_out}));  // open: cin, cout
  Multiplexer #(.enable("false"), .width(4)) multiplexer_1 (
    .in0(if_id_1_instructionout[11:8]), .in1(if_id_1_instructionout[7:4]), .out(multiplexer_1_out),
    .sel(control_unit_1_regdest));
  assign bit_extender_1_out = {{4{if_id_1_instructionout[3]}}, if_id_1_instructionout[3:0]};  // Bit_Extender bit_extender_1
  Control_Unit control_unit_1 (
    .Opcode(if_id_1_instructionout[19:16]), .ALUop(control_unit_1_aluop), .ALUsrc(control_unit_1_alusrc),
    .RegDest(control_unit_1_regdest), .MemToReg(control_unit_1_memtoreg), .MemRead(control_unit_1_memread),
    .MemWrite(control_unit_1_memwrite), .RegWrite(control_unit_1_regwrite), .Shift(control_unit_1_shift));  // open: jmp, bneq, beq
  RegisterMem registermem_1 (
    .regWrite(mem_wb_1_r_write_out), .rreg1(if_id_1_instructionout[15:12]),
    .rreg2(if_id_1_instructionout[11:8]), .wreg(mem_wb_1_wb_reg_out), .wval(mem_wb_1_write_data_out),
    .CLK(CLK), .Reset(ResetPC), .rval1(registermem_1_rval1), .rval2(registermem_1_rval2));
  Multiplexer #(.enable("false"), .width(8)) multiplexer_2 (
    .in0(registermem_1_rval2), .in1(if_id_1_instructionout[7:0]), .out(multiplexer_2_out),
    .sel(control_unit_1_alusrc));
  Multiplexer #(.enable("false"), .width(8)) multiplexer_3 (
    .in0(registermem_1_rval1), .in1(bit_extender_1_out), .out(multiplexer_3_out), .sel(control_unit_1_shift));
  ID_EX_REGISTER id_ex_register_1 (
    .ENABLE(1'b1), .CLK(CLK), .RESET(ResetPC), .REG_ONE_READ_P(if_id_1_instructionout[15:12]),
    .REG_ONE_VAL_P(multiplexer_3_out), .REG_TWO_READ_P(if_id_1_instructionout[11:8]),
    .REG_TWO_VAL_P(multiplexer_2_out), .REG_WRITE_ADDRESS_P(multiplexer_1_out),
    .REG_WRITE_VAL_P(multiplexer_8_out), .SIGN_EXTEND_P(bit_extender_1_out), .ALU_OP_P(control_unit_1_aluop),
    .ALU_A_P(registermem_1_rval1), .ALU_B_P(registermem_1_rval2), .ALU_SRC_P(control_unit_1_alusrc),
    .REG_DES_P(control_unit_1_regdest), .MEM_TO_REG_P(control_unit_1_memtoreg),
    .MEM_READ_P(control_unit_1_memread), .MEM_WRITE_P(control_unit_1_memwrite),
    .REG_WRITE_P(control_unit_1_regwrite), .SHIFT_P(control_unit_1_shift),
    .REG_ONE_READ_P2(id_ex_register_1_reg_one_read_p2), .REG_ONE_VAL_P2(id_ex_register_1_reg_one_val_p2),
    .REG_TWO_READ_P2(id_ex_register_1_reg_two_read_p2), .REG_TWO_VAL_P2(id_ex_register_1_reg_two_val_p2),
    .REG_WRITE_ADDRESS_P2(id_ex_register_1_reg_write_address_p2), .ALU_OP_P2(id_ex_register_1_alu_op_p2),
    .MEM_TO_REG_P2(id_ex_register_1_mem_to_reg_p2), .MEM_READ_P2(id_ex_register_1_mem_read_p2),
    .MEM_WRITE_P2(id_ex_register_1_mem_write_p2), .REG_WRITE_P2(id_ex_register_1_reg_write_p2));  // open: in_21, REG_WRITE_VAL_P2, SIGN_EXTEND_P2, ALU_A_P2, ALU_B_P2, ALU_SRC_P2, REG_DES_P2, SHIFT_P2, out_39
  ALU alu_1 (
    .ALUop(id_ex_register_1_alu_op_p2), .A(multiplexer_4_out), .B(multiplexer_5_out), .Zero(alu_1_zero),
    .ALUOUT(alu_1_aluout));
  assign bit_extender_2_out = {{4{undriven[7]}}, undriven};  // Bit_Extender bit_extender_2
  Forwarding_Unit forwarding_unit_1 (
    .EX_MEM_Reg_Write(ex_mem_1_regwrite_out), .MEM_WB_Reg_Write(mem_wb_1_r_write_out),
    .EX_MEM_RD(ex_mem_1_write_reg_out), .MEM_WB_RD(mem_wb_1_wb_reg_out),
    .ID_EX_A(id_ex_register_1_reg_one_read_p2), .ID_EX_B(id_ex_register_1_reg_two_read_p2),
    .Forward_A(forwarding_unit_1_forward_a), .Forward_B(forwarding_unit_1_forward_b));
  Adder #(.width(12)) adder_2 (
    .a({adder_1_out_2, adder_1_out}), .b(bit_extender_2_out), .out(adder_2_out));  // open: cin, cout
  not not_1 (not_1_out, undriven_2);
  buf and_1 (and_1_out, not_1_out);  // AND_Gate
  buf and_2 (and_2_out, undriven_2);  // AND_Gate
  Multiplexer #(.enable("false"), .select(2), .width(8)) multiplexer_4 (
    .in0(id_ex_register_1_reg_one_val_p2), .in1(mem_wb_1_write_data_out), .in2(ex_mem_1_alu_result_out),
    .out(multiplexer_4_out), .sel(forwarding_unit_1_forward_a));  // open: in3
  Multiplexer #(.enable("false"), .select(2), .width(8)) multiplexer_5 (
    .in0(id_ex_register_1_reg_two_val_p2), .in1(mem_wb_1_write_data_out), .in2(ex_mem_1_alu_result_out),
    .out(multiplexer_5_out), .sel(forwarding_unit_1_forward_b));  // open: in3
  Multiplexer #(.enable("false"), .width(12)) multiplexer_6 (
    .in0({adder_1_out_2, adder_1_out}), .in1(adder_2_out), .out(multiplexer_6_out), .sel(or_1_out));
  or or_1 (or_1_out, and_1_out, and_2_out);
  Multiplexer #(.enable("false"), .width(12)) multiplexer_7 (
    .in0(multiplexer_6_out), .in1({adder_1_out_2, if_id_1_instructionout[15:8]}), .out(multiplexer_7_out));  // open: sel
  Ex_mem ex_mem_1 (
    .MemToReg(id_ex_register_1_mem_to_reg_p2), .MemRead(id_ex_register_1_mem_read_p2),
    .MemWrite(id_ex_register_1_mem_write_p2), .RegWrite(id_ex_register_1_reg_write_p2),
    .ZeroFlag(alu_1_zero), .ALU_result(alu_1_aluout), .WriteReg(id_ex_register_1_reg_write_address_p2),
    .CLK(CLK), .Reset(ResetPC), .MemtoReg_out(ex_mem_1_memtoreg_out), .MemRead_out(ex_mem_1_memread_out),
    .MemWrite_out(ex_mem_1_memwrite_out), .RegWrite_out(ex_mem_1_regwrite_out),
    .ALU_result_out(ex_mem_1_alu_result_out), .Write_reg_out(ex_mem_1_write_reg_out));  // open: ZeroFlag_out
  DataMemory datamemory_1 (
    .MemoryAddress(alu_1_aluout), .MemWrite(ex_mem_1_memwrite_out), .MemRead(ex_mem_1_memread_out),
    .CLK(CLK), .WriteData(registermem_1_rval2), .ReadData(datamemory_1_readdata));
  Multiplexer #(.enable("false"), .width(8)) multiplexer_8 (
    .in0(alu_1_aluout), .in1(datamemory_1_readdata), .out(multiplexer_8_out), .sel(ex_mem_1_memtoreg_out));
  MEM_WB mem_wb_1 (
    .R_write_in(ex_mem_1_regwrite_out), .CLK(CLK), .WB_REG_IN(ex_mem_1_write_reg_out),
    .ALU_RESULT_IN(ex_mem_1_alu_result_out), .WRITE_DATA_IN(ex_mem_1_alu_result_out), .RESET(ResetPC),
    .R_write_out(mem_wb_1_r_write_out), .WB_REG_OUT(mem_wb_1_wb_reg_out),
    .WRITE_DATA_OUT(mem_wb_1_write_data_out), .CLK_WRITE(mem_wb_1_clk_write));  // open: MEM_DATA_IN, Mem2RegIn, MEM_DATA_OUT, ALU_RESULT_OUT, Mem2RegOut
endmodule
