// Logisim project Ex_Mem_Register.circ as structural Verilog
module Ex_mem (
  input  MemToReg,
  input  MemRead,
  input  MemWrite,
  input  RegWrite,
  input  ZeroFlag,
  input  [7:0] ALU_result,
  input  [3:0] WriteReg,
  input  Reset,
  output MemtoReg_out,
  output MemRead_out,
  output MemWrite_out,
  output RegWrite_out,
  output ZeroFlag_out,
  output [7:0] ALU_result_out,
  output [3:0] out_15
);

  wire clock_1_out;

  Clock clock_1 (.out(clock_1_out));
  Register #(.width(1)) register_1 (.D(MemToReg), .en(1'b1), .clk(clock_1_out), .Q(MemtoReg_out), .clr(Reset));
  Register #(.width(1)) register_2 (.D(MemRead), .en(1'b1), .clk(clock_1_out), .Q(MemRead_out), .clr(Reset));
  Register #(.width(1)) register_3 (.D(MemWrite), .en(1'b1), .clk(clock_1_out), .Q(MemWrite_out), .clr(Reset));
  Register #(.width(1)) register_4 (.D(RegWrite), .en(1'b1), .clk(clock_1_out), .Q(RegWrite_out), .clr(Reset));
  Register #(.width(1)) register_5 (.D(ZeroFlag), .en(1'b1), .clk(clock_1_out), .Q(ZeroFlag_out), .clr(Reset));
  Register register_6 (.D(ALU_result), .en(1'b1), .clk(clock_1_out), .Q(ALU_result_out), .clr(Reset));
  Register #(.width(4)) register_7 (.D(WriteReg), .en(1'b1), .clk(clock_1_out), .Q(out_15), .clr(Reset));
endmodule
