// Logisim project ID_EX.circ as structural Verilog: 1 circuit, main circuit ID_EX_REGISTER
module ID_EX_REGISTER (
  input  ENABLE,
  input  CLK,
  input  RESET,
  input  [3:0] REG_ONE_READ_P,
  input  [7:0] REG_TWO_READ_P,
  input  [3:0] REG_ONE_VAL_P,
  input  [7:0] REG_TWO_VAL_P,
  input  [3:0] REG_WRITE_ADDRESS_P,
  input  [7:0] REG_WRITE_VAL_P,
  input  [7:0] SIGN_EXTEND_P,
  input  [2:0] ALU_OP_P,
  input  [7:0] ALU_A_P,
  input  [7:0] ALU_B_P,
  input  ALU_SRC_P,
  input  REG_DES_P,
  input  MEM_TO_REG_P,
  input  MEM_READ_P,
  input  MEM_WRITE_P,
  input  REG_WRITE_P,
  input  SHIFT_P,
  input  in_21,
  output [3:0] REG_ONE_READ_P2,
  output [7:0] REG_TWO_READ_P2,
  output [3:0] REG_ONE_VAL_P2,
  output [7:0] REG_TWO_VAL_P2,
  output [3:0] REG_WRITE_ADDRESS_P2,
  output [7:0] REG_WRITE_VAL_P2,
  output [7:0] SIGN_EXTEND_P2,
  output [2:0] ALU_OP_P2,
  output [7:0] ALU_A_P2,
  output [7:0] ALU_B_P2,
  output ALU_SRC_P2,
  output REG_DES_P2,
  output MEM_TO_REG_P2,
  output MEM_READ_P2,
  output MEM_WRITE_P2,
  output REG_WRITE_P2,
  output SHIFT_P2,
  output out_39
);

  Register #(.width(4)) REG_ONE_READ (.D(REG_ONE_READ_P), .en(ENABLE), .clk(CLK), .Q(REG_ONE_READ_P2), .clr(RESET));
  Register REG_TWO_READ (.D(REG_TWO_READ_P), .en(ENABLE), .clk(CLK), .Q(REG_TWO_READ_P2), .clr(RESET));
  Register #(.width(4)) REG_ONE_VAL (.D(REG_ONE_VAL_P), .en(ENABLE), .clk(CLK), .Q(REG_ONE_VAL_P2), .clr(RESET));
  Register REG_TWO_VAL (.D(REG_TWO_VAL_P), .en(ENABLE), .clk(CLK), .Q(REG_TWO_VAL_P2), .clr(RESET));
  Register #(.width(4)) REG_WRITE_ADDRESS (
    .D(REG_WRITE_ADDRESS_P), .en(ENABLE), .clk(CLK), .Q(REG_WRITE_ADDRESS_P2), .clr(RESET));
  Register REG_WRITE_VAL (.D(REG_WRITE_VAL_P), .clk(CLK), .Q(REG_WRITE_VAL_P2), .clr(RESET));  // open: en
  Register SIGN_EXTEND (.D(SIGN_EXTEND_P), .en(ENABLE), .clk(CLK), .Q(SIGN_EXTEND_P2), .clr(RESET));
  Register #(.width(3)) ALU_OP (.D(ALU_OP_P), .en(ENABLE), .clk(CLK), .Q(ALU_OP_P2), .clr(RESET));
  Register ALU_A (.D(ALU_A_P), .en(ENABLE), .clk(CLK), .Q(ALU_A_P2), .clr(RESET));
  Register ALU_B (.D(ALU_B_P), .en(ENABLE), .clk(CLK), .Q(ALU_B_P2), .clr(RESET));
  Register #(.width(1)) ALU_SRC (.D(ALU_SRC_P), .en(ENABLE), .clk(CLK), .Q(ALU_SRC_P2), .clr(RESET));
  Register #(.width(1)) REG_DES (.D(REG_DES_P), .clk(CLK), .Q(REG_DES_P2), .clr(RESET));  // open: en
  Register #(.width(1)) MEM_TO_REG (.D(MEM_TO_REG_P), .en(ENABLE), .clk(CLK), .Q(MEM_TO_REG_P2), .clr(RESET));
  Register #(.width(1)) MEM_READ (.D(MEM_READ_P), .en(ENABLE), .clk(CLK), .Q(MEM_READ_P2), .clr(RESET));
  Register #(.width(1)) MEM_WRITE (.D(MEM_WRITE_P), .en(ENABLE), .clk(CLK), .Q(MEM_WRITE_P2), .clr(RESET));
  Register #(.width(1)) REG_WRITE (.D(REG_WRITE_P), .en(ENABLE), .clk(CLK), .Q(REG_WRITE_P2), .clr(RESET));
  Register #(.width(1)) SHIFT (.D(SHIFT_P), .en(ENABLE), .clk(CLK), .Q(SHIFT_P2), .clr(RESET));
  Register #(.width(1)) register_1 (.D(in_21), .clk(CLK), .Q(out_39), .clr(RESET));  // open: en
endmodule
