// Logisim project MIPS.circ as structural Verilog: 6 circuits, main circuit main
module main (
  input  ResetPC
);

  wire alu_1_zero, and_1_out, and_2_out, CLK_out, control_unit_1_alusrc, control_unit_1_beq,
       control_unit_1_bneq, control_unit_1_jmp, control_unit_1_memread, control_unit_1_memtoreg,
       control_unit_1_memwrite, control_unit_1_regdest, control_unit_1_regwrite, control_unit_1_shift,
       not_1_out, or_1_out;
  wire [2:0] control_unit_1_aluop;
  wire [3:0] multiplexer_1_out;
  wire [7:0] alu_1_aluout, bit_extender_1_out, datamemory_1_readdata, instructionmem_1_out_2_2,
       multiplexer_2_out, multiplexer_3_out, multiplexer_6_out, registermem_1_rval1, registermem_1_rval2;
  wire [11:0] adder_1_out, adder_2_out, bit_extender_2_out, multiplexer_4_out, multiplexer_5_out, PC_q;
  wire [19:0] instructionmem_1_out_2;

  Register #(.width(12)) PC (.D(multiplexer_5_out), .en(1'b1), .clk(CLK_out), .Q(PC_q), .clr(ResetPC));
  Clock CLK (.out(CLK_out));
  Adder #(.width(12)) adder_1 (.a(PC_q), .b(12'h1), .out(adder_1_out));  // open: cin, cout
  InstructionMem instructionmem_1 (
    .in_1(PC_q),
    .out_2({instructionmem_1_out_2[19:16], instructionmem_1_out_2_2, instructionmem_1_out_2[7:0]}));
  Multiplexer #(.enable("false"), .width(4)) multiplexer_1 (
    .in0(instructionmem_1_out_2_2[3:0]), .in1(instructionmem_1_out_2[7:4]), .out(multiplexer_1_out),
    .sel(control_unit_1_regdest));
  assign bit_extender_1_out = {{4{instructionmem_1_out_2[3]}}, instructionmem_1_out_2[3:0]};  // Bit_Extender bit_extender_1
  Control_Unit control_unit_1 (
    .Opcode(instructionmem_1_out_2[19:16]), .ALUop(control_unit_1_aluop), .jmp(control_unit_1_jmp),
    .bneq(control_unit_1_bneq), .beq(control_unit_1_beq), .ALUsrc(control_unit_1_alusrc),
    .RegDest(control_unit_1_regdest), .MemToReg(control_unit_1_memtoreg), .MemRead(control_unit_1_memread),
    .MemWrite(control_unit_1_memwrite), .RegWrite(control_unit_1_regwrite), .Shift(control_unit_1_shift));
  RegisterMem registermem_1 (
    .regWrite(control_unit_1_regwrite), .rreg1(instructionmem_1_out_2_2[7:4]),
    .rreg2(instructionmem_1_out_2_2[3:0]), .wreg(multiplexer_1_out), .wval(multiplexer_6_out), .CLK(CLK_out),
    .in_7(ResetPC), .rval1(registermem_1_rval1), .rval2(registermem_1_rval2));
  Multiplexer #(.enable("false"), .width(8)) multiplexer_2 (
    .in0(registermem_1_rval1), .in1(bit_extender_1_out), .out(multiplexer_2_out), .sel(control_unit_1_shift));
  Multiplexer #(.enable("false"), .width(8)) multiplexer_3 (
    .in0(registermem_1_rval2), .in1(instructionmem_1_out_2[7:0]), .out(multiplexer_3_out),
    .sel(control_unit_1_alusrc));
  assign bit_extender_2_out = {{4{instructionmem_1_out_2[7]}}, instructionmem_1_out_2[7:0]};  // Bit_Extender bit_extender_2
  Adder #(.width(12)) adder_2 (.a(adder_1_out), .b(bit_extender_2_out), .out(adder_2_out));  // open: cin, cout
  not not_1 (not_1_out, alu_1_zero);
  ALU alu_1 (
    .ALUop(control_unit_1_aluop), .A(multiplexer_2_out), .B(multiplexer_3_out), .Zero(alu_1_zero),
    .ALUOUT(alu_1_aluout));
  and and_1 (and_1_out, not_1_out, control_unit_1_bneq);
  and and_2 (and_2_out, control_unit_1_beq, alu_1_zero);
  Multiplexer #(.enable("false"), .width(12)) multiplexer_4 (
    .in0(adder_1_out), .in1(adder_2_out), .out(multiplexer_4_out), .sel(or_1_out));
  or or_1 (or_1_out, and_1_out, and_2_out);
  Multiplexer #(.enable("false"), .width(12)) multiplexer_5 (
    .in0(multiplexer_4_out), .in1({adder_1_out[11:8], instructionmem_1_out_2_2}), .out(multiplexer_5_out),
    .sel(control_unit_1_jmp));
  DataMemory datamemory_1 (
    .MemoryAddress(alu_1_aluout), .MemWrite(control_unit_1_memwrite), .MemRead(control_unit_1_memread),
    .CLK(CLK_out), .WriteData(registermem_1_rval2), .ReadData(datamemory_1_readdata));
  Multiplexer #(.enable("false"), .width(8)) multiplexer_6 (
    .in0(alu_1_aluout), .in1(datamemory_1_readdata), .out(multiplexer_6_out), .sel(control_unit_1_memtoreg));
endmodule

module Control_Unit (
  input  [3:0] Opcode,
  output [2:0] ALUop,
  output jmp,
  output bneq,
  output beq,
  output ALUsrc,
  output RegDest,
  output MemToReg,
  output MemRead,
  output MemWrite,
  output RegWrite,
  output Shift
);

  ROM #(.addrWidth(4), .dataWidth(13)) rom_1 (
    .addr(Opcode),
    .data({Shift, RegWrite, MemWrite, MemRead, MemToReg, RegDest, ALUsrc, beq, bneq, jmp, ALUop}));

  // Notes on the sheet:
  //   contents of rom_1 (hex, n*v repeats v):
  //   b40 1885 881 842 840 841 843 440 11 880 882 1886 884 f 21 883
endmodule

// t7
module RegisterMem (
  input  regWrite,
  input  [3:0] rreg1,
  input  [3:0] rreg2,
  input  [3:0] wreg,
  input  [7:0] wval,
  input  CLK,
  input  in_7,
  output [7:0] rval1,
  output [7:0] rval2
);

  wire demultiplexer_1_out0, demultiplexer_1_out1, demultiplexer_1_out2, demultiplexer_1_out3,
       demultiplexer_1_out4, demultiplexer_1_out5, demultiplexer_1_out6, demultiplexer_1_out7;
  wire [7:0] SP_q, t0_q, t1_q, t2_q, t3_q, t4_q, t6_q, zero_q;

  Demultiplexer #(.enable("false"), .select(4)) demultiplexer_1 (
    .out0(demultiplexer_1_out0), .out1(demultiplexer_1_out1), .out2(demultiplexer_1_out2),
    .out3(demultiplexer_1_out3), .out4(demultiplexer_1_out4), .out5(demultiplexer_1_out5),
    .out6(demultiplexer_1_out6), .out7(demultiplexer_1_out7), .in(regWrite), .sel(wreg));  // open: out8, out9, out10, out11, out12, out13, out14, out15
  Register t0 (.D(wval), .en(demultiplexer_1_out0), .clk(CLK), .Q(t0_q), .clr(in_7));
  Register t1 (.D(wval), .en(demultiplexer_1_out1), .clk(CLK), .Q(t1_q), .clr(in_7));
  Register t2 (.D(wval), .en(demultiplexer_1_out2), .clk(CLK), .Q(t2_q), .clr(in_7));
  Register t3 (.D(wval), .en(demultiplexer_1_out3), .clk(CLK), .Q(t3_q), .clr(in_7));
  Register t4 (.D(wval), .en(demultiplexer_1_out4), .clk(CLK), .Q(t4_q), .clr(in_7));
  Register zero (.D({8{1'b0}}), .en(demultiplexer_1_out5), .clk(CLK), .Q(zero_q), .clr(in_7));
  Register SP (.D(wval), .en(demultiplexer_1_out6), .clk(CLK), .Q(SP_q));  // open: clr
  Register t6 (.D(wval), .en(demultiplexer_1_out7), .clk(CLK), .Q(t6_q));  // open: clr
  Multiplexer #(.enable("false"), .select(4), .width(8)) multiplexer_1 (
    .in0(t0_q), .in1(t1_q), .in2(t2_q), .in3(t3_q), .in4(t4_q), .in5(zero_q), .in6(SP_q), .in7(t6_q),
    .out(rval1), .sel(rreg1));  // open: in8, in9, in10, in11, in12, in13, in14, in15
  Multiplexer #(.enable("false"), .select(4), .width(8)) multiplexer_2 (
    .in0(t0_q), .in1(t1_q), .in2(t2_q), .in3(t3_q), .in4(t4_q), .in5(zero_q), .in6(SP_q), .in7(t6_q),
    .out(rval2), .sel(rreg2));  // open: in8, in9, in10, in11, in12, in13, in14, in15
endmodule

module DataMemory (
  input  [7:0] MemoryAddress,
  input  MemWrite,
  input  MemRead,
  input  CLK,
  input  [7:0] WriteData,
  output [7:0] ReadData
);

  RAM #(.asyncread("true")) ram_1 (
    .addr(MemoryAddress), .we(MemWrite), .oe(MemRead), .clk(CLK), .din(WriteData), .dout(ReadData));
endmodule

module InstructionMem (
  input  [11:0] in_1,
  output [19:0] out_2
);

  ROM #(.addrWidth(12), .dataWidth(20)) rom_1 (.addr(in_1), .data(out_2));

  // Notes on the sheet:
  //   contents of rom_1 (hex, n*v repeats v):
  //   1003 71004
endmodule

module ALU (
  input  [2:0] ALUop,
  input  [7:0] A,
  input  [7:0] B,
  output Zero,
  output [7:0] ALUOUT
);

  wire [7:0] adder_1_out, and_1_out, nor_1_out, or_1_out, shifter_1_out, shifter_2_out, subtractor_1_out;

  Adder adder_1 (.a(A), .b(B), .out(adder_1_out));  // open: cin, cout
  Subtractor subtractor_1 (.a(A), .b(B), .out(subtractor_1_out));  // open: bin, bout
  assign and_1_out = A & B;  // AND_Gate and_1, 8 bits wide
  assign or_1_out = A | B;  // OR_Gate or_1, 8 bits wide
  assign nor_1_out = ~(A | B);  // NOR_Gate nor_1, 8 bits wide
  Shifter shifter_1 (.in(B), .\dist (A[2:0]), .out(shifter_1_out));
  Shifter #(.shift("lr")) shifter_2 (.in(B), .\dist (A[2:0]), .out(shifter_2_out));
  Multiplexer #(.enable("false"), .select(3), .width(8)) multiplexer_1 (
    .in0(adder_1_out), .in1(subtractor_1_out), .in2(or_1_out), .in3(and_1_out), .in4(nor_1_out),
    .in5(shifter_1_out), .in6(shifter_2_out), .out(ALUOUT), .sel(ALUop));  // open: in7
  Comparator comparator_1 (.a({8{1'b0}}), .b(ALUOUT), .eq(Zero));  // open: gt, lt
endmodule
