// Logisim project Main.circ as structural Verilog: 5 circuits, main circuit main
module main (
  input  [15:0] in_1,
  input  [15:0] in_2,
  output [15:0] out_3,
  output UnderFlow,
  output Overflow
);

  finalAdder Adder (.in_1(in_1), .in_2(in_2), .Result(out_3), .UF(UnderFlow), .OF(Overflow));
endmodule

module finalAdder (
  input  [15:0] in_1,
  input  [15:0] in_2,
  output [15:0] Result,
  output UF,
  output OF
);

  wire comparator_1_eq, fp_preprocessor_b09eaee1_1_p3, fp_preprocessor_b09eaee1_1_p4,
       fp_preprocessor_b09eaee1_1_p5, fp_preprocessor_b09eaee1_1_p6, fp_preprocessor_b09eaee1_1_p7,
       ieee_adder_f7459b58_1_p6, ieee_adder_f7459b58_1_p7, or_1_out;
  wire [3:0] ieee_adder_f7459b58_1_p9, normalizer_1_expout, shiftamount_1_shiftamount;
  wire [15:0] ieee_adder_f7459b58_1_p8, normalizer_1_fracout;

  // fp_preprocessor_b09eaee1 fp_preprocessor_b09eaee1_1: pin names not known; wires that end beside it: in_1, in_2, fp_preprocessor_b09eaee1_1_p3, fp_preprocessor_b09eaee1_1_p4, fp_preprocessor_b09eaee1_1_p5, fp_preprocessor_b09eaee1_1_p6, fp_preprocessor_b09eaee1_1_p7
  // IEEE_Adder_f7459b58 ieee_adder_f7459b58_1: pin names not known; wires that end beside it: fp_preprocessor_b09eaee1_1_p5, fp_preprocessor_b09eaee1_1_p6, fp_preprocessor_b09eaee1_1_p4, fp_preprocessor_b09eaee1_1_p7, fp_preprocessor_b09eaee1_1_p3, ieee_adder_f7459b58_1_p6, ieee_adder_f7459b58_1_p7, ieee_adder_f7459b58_1_p8, ieee_adder_f7459b58_1_p9
  ShiftAmount shiftamount_1 (.FracIn(ieee_adder_f7459b58_1_p8), .ShiftAmount(shiftamount_1_shiftamount));
  Normalizer normalizer_1 (
    .Fraction(ieee_adder_f7459b58_1_p8), .Exp(ieee_adder_f7459b58_1_p9),
    .ShiftAmount(shiftamount_1_shiftamount), .FracOut(normalizer_1_fracout), .ExpOut(normalizer_1_expout),
    .Underflow(UF));
  Truncate truncate_1 (
    .Sign(ieee_adder_f7459b58_1_p7), .Exp(normalizer_1_expout), .Frac(normalizer_1_fracout), .out_4(Result));
  Comparator #(.width(4)) comparator_1 (.a(normalizer_1_expout), .b(4'b1111), .eq(comparator_1_eq));  // open: gt, lt
  or or_1 (or_1_out, ieee_adder_f7459b58_1_p6, comparator_1_eq);
  Multiplexer #(.enable("false")) multiplexer_1 (.in0(or_1_out), .in1(1'b0), .out(OF), .sel(UF));
endmodule

// Normalize
module Normalizer (
  input  [15:0] Fraction,
  input  [3:0] Exp,
  input  [3:0] ShiftAmount,
  output [15:0] FracOut,
  output [3:0] ExpOut,
  output Underflow
);

  wire comparator_1_eq, subtractor_1_bout;

  Shifter #(.width(16)) shifter_1 (.in(Fraction), .\dist (ShiftAmount), .out(FracOut));
  Subtractor #(.width(4)) subtractor_1 (.a(Exp), .b(ShiftAmount), .out(ExpOut), .bout(subtractor_1_bout));  // open: bin
  Comparator #(.width(4)) comparator_1 (.a(ShiftAmount), .b(Exp), .eq(comparator_1_eq));  // open: gt, lt
  or or_1 (Underflow, subtractor_1_bout, comparator_1_eq);
endmodule

// ShiftCnt
module ShiftAmount (
  input  [15:0] FracIn,
  output [3:0] ShiftAmount
);

  BitFinder #(.width(16)) bitfinder_1 (
    .in({FracIn[0], FracIn[1], FracIn[2], FracIn[3], FracIn[4], FracIn[5], FracIn[6], FracIn[7], FracIn[8], FracIn[9], FracIn[10], FracIn[11], FracIn[12], FracIn[13], FracIn[14], FracIn[15]}),
    .index(ShiftAmount));  // open: found
endmodule

module Truncate (
  input  Sign,
  input  [3:0] Exp,
  input  [15:0] Frac,
  output [15:0] out_4
);


  assign out_4 = {Sign, Exp, Frac[14:4]};
endmodule
