// Logisim project Preprocessing.circ as structural Verilog
module Comparer (
  input  [3:0] exponent__a,
  input  [3:0] exponent__b,
  output [3:0] exponent_diff,
  output exp_a___exp_b
);

  wire subtractor_1_bout, undriven;
  wire [3:0] negator_1_out, subtractor_1_out;

  Subtractor #(.width(4)) subtractor_1 (
    .a(exponent__a), .b(exponent__b), .out(subtractor_1_out), .bin(undriven), .bout(subtractor_1_bout));
  Negator #(.width(4)) negator_1 (.in(subtractor_1_out), .out(negator_1_out));
  not not_1 (exp_a___exp_b, subtractor_1_bout);
  Multiplexer #(.width(4)) multiplexer_1 (
    .in0(subtractor_1_out), .in1(negator_1_out), .out(exponent_diff), .sel(subtractor_1_bout));  // open: en
endmodule

module padder (
  input  [10:0] input_frac,
  input  [3:0] input_exp,
  output [15:0] padded_frac,
  output [3:0] exp
);

  or or_1 (padded_frac[15], input_exp[0], input_exp[1], input_exp[2], input_exp[2], input_exp[3]);
  Multiplexer #(.width(4), .enable("false")) multiplexer_1 (
    .in0(4'b0001), .in1(input_exp), .out(exp), .sel(padded_frac[15]));

  assign padded_frac[14:0] = {input_frac, 4'b0000};

  // Notes on the sheet:
  //   LMB = 0, not used
endmodule

module fp_preprocessor (
  input  [15:0] input_a,
  input  [15:0] input_b,
  output [15:0] padded_frac_a,
  output [15:0] padded_frac_b,
  output [15:0] shifted_frac_a,
  output [15:0] shifted_frac_b,
  output [3:0] exp,
  output sign_a,
  output sign_b
);

  wire comparer_1_exp_a___exp_b;
  wire [3:0] bit_splitter_1_exp, bit_splitter_2_exp, comparer_1_exponent_diff, padder_1_exp, padder_2_exp;
  wire [10:0] bit_splitter_1_frac, bit_splitter_2_frac;

  padder padder_1 (
    .input_frac(bit_splitter_1_frac), .input_exp(bit_splitter_1_exp), .exp(padder_1_exp),
    .padded_frac(padded_frac_b));
  bit_splitter bit_splitter_1 (.in_1(input_b), .sign(sign_b), .exp(bit_splitter_1_exp), .frac(bit_splitter_1_frac));
  frac_shifter frac_shifter_1 (
    .shift_anount(comparer_1_exponent_diff), .exponent_a___b(comparer_1_exp_a___exp_b),
    .exp__a(padder_2_exp), .exp__b(padder_1_exp), .padded__frac_a(padded_frac_a),
    .padded__frac_b(padded_frac_b), .bigger_exp(exp), .out_frac_a(shifted_frac_a), .out_frac_b(shifted_frac_b));
  bit_splitter bit_splitter_2 (.in_1(input_a), .sign(sign_a), .exp(bit_splitter_2_exp), .frac(bit_splitter_2_frac));
  padder padder_2 (
    .input_frac(bit_splitter_2_frac), .input_exp(bit_splitter_2_exp), .exp(padder_2_exp),
    .padded_frac(padded_frac_a));
  Comparer comparer_1 (
    .exponent__a(bit_splitter_2_exp), .exponent__b(bit_splitter_1_exp),
    .exponent_diff(comparer_1_exponent_diff), .exp_a___exp_b(comparer_1_exp_a___exp_b));
endmodule

module bit_splitter (
  input  [15:0] in_1,
  output sign,
  output [10:0] frac,
  output [3:0] exp
);


  assign exp = in_1[14:11];
  assign frac = in_1[10:0];
  assign sign = in_1[15];
endmodule

module frac_shifter (
  input  [3:0] shift_anount,
  input  exponent_a___b,
  input  [3:0] exp__a,
  input  [3:0] exp__b,
  input  [15:0] padded__frac_a,
  input  [15:0] padded__frac_b,
  output [3:0] bigger_exp,
  output [15:0] out_frac_a,
  output [15:0] out_frac_b
);

  wire [15:0] shifter_1_out, shifter_2_out;

  Shifter #(.width(16), .shift("lr")) shifter_1 (.in(padded__frac_a), .\dist (shift_anount), .out(shifter_1_out));
  Shifter #(.width(16), .shift("lr")) shifter_2 (.in(padded__frac_b), .\dist (shift_anount), .out(shifter_2_out));
  Multiplexer #(.width(16), .enable("false")) multiplexer_1 (
    .in0(shifter_1_out), .in1(padded__frac_a), .out(out_frac_a), .sel(exponent_a___b));
  Multiplexer #(.width(16), .enable("false")) multiplexer_2 (
    .in0(padded__frac_b), .in1(shifter_2_out), .out(out_frac_b), .sel(exponent_a___b));
  Multiplexer #(.width(4), .enable("false")) multiplexer_3 (
    .in0(exp__b), .in1(exp__a), .out(bigger_exp), .sel(exponent_a___b));
endmodule
